// Logisim project improved-ball-movement.circ as structural Verilog: 1 circuit, main circuit main
module main (
);

  wire d_ff_1_q, isDown, power, register_2_q;
  wire [4:0] counter_1_q, dmx_x_cord;
  wire [7:0] adder_1_out, divider_1_out, multiplexer_1_out, multiplexer_2_out, register_1_q, subtractor_1_out;
  wire [31:0] decoder_2_out0, demultiplexer_1_out0, demultiplexer_1_out1, demultiplexer_1_out2,
       demultiplexer_1_out3, demultiplexer_1_out4, demultiplexer_1_out5, demultiplexer_1_out6,
       demultiplexer_1_out7, demultiplexer_1_out8, demultiplexer_1_out9, demultiplexer_1_out10,
       demultiplexer_1_out11, demultiplexer_1_out12, demultiplexer_1_out13, demultiplexer_1_out14,
       demultiplexer_1_out15, demultiplexer_1_out16, demultiplexer_1_out17, demultiplexer_1_out18,
       demultiplexer_1_out19, demultiplexer_1_out20, demultiplexer_1_out21, demultiplexer_1_out22,
       demultiplexer_1_out23, demultiplexer_1_out24, demultiplexer_1_out25, demultiplexer_1_out26,
       demultiplexer_1_out27, demultiplexer_1_out28, demultiplexer_1_out29, demultiplexer_1_out30,
       demultiplexer_1_out31, dmx_y_cord;

  Clock clock_1 (.out(power));
  D_Flip_Flop d_ff_1 (.Q(d_ff_1_q), .preset(decoder_2_out0[31]), .reset(decoder_2_out0[0]));  // open: clk, D, Qn, en
  Register register_1 (.D(multiplexer_2_out), .Q(register_1_q), .clk(power));  // open: en, clr
  DotMatrix #(.matrixcols(32), .matrixrows(32)) dotmatrix_1 (
    .col0(demultiplexer_1_out0), .col1(demultiplexer_1_out1), .col2(demultiplexer_1_out2),
    .col3(demultiplexer_1_out3), .col4(demultiplexer_1_out4), .col5(demultiplexer_1_out5),
    .col6(demultiplexer_1_out6), .col7(demultiplexer_1_out7), .col8(demultiplexer_1_out8),
    .col9(demultiplexer_1_out9), .col10(demultiplexer_1_out10), .col11(demultiplexer_1_out11),
    .col12(demultiplexer_1_out12), .col13(demultiplexer_1_out13), .col14(demultiplexer_1_out14),
    .col15(demultiplexer_1_out15), .col16(demultiplexer_1_out16), .col17(demultiplexer_1_out17),
    .col18(demultiplexer_1_out18), .col19(demultiplexer_1_out19), .col20(demultiplexer_1_out20),
    .col21(demultiplexer_1_out21), .col22(demultiplexer_1_out22), .col23(demultiplexer_1_out23),
    .col24(demultiplexer_1_out24), .col25(demultiplexer_1_out25), .col26(demultiplexer_1_out26),
    .col27(demultiplexer_1_out27), .col28(demultiplexer_1_out28), .col29(demultiplexer_1_out29),
    .col30(demultiplexer_1_out30), .col31(demultiplexer_1_out31));
  Multiplexer #(.select(3), .width(8)) multiplexer_1 (
    .in2(8'h1), .in3(8'h2), .in4(8'h6), .in5(8'h8), .out(multiplexer_1_out), .sel(3'b010));  // open: in0, in1, in6, in7, en
  Demultiplexer #(.select(5), .width(32)) demultiplexer_1 (
    .out0(demultiplexer_1_out0), .out1(demultiplexer_1_out1), .out2(demultiplexer_1_out2),
    .out3(demultiplexer_1_out3), .out4(demultiplexer_1_out4), .out5(demultiplexer_1_out5),
    .out6(demultiplexer_1_out6), .out7(demultiplexer_1_out7), .out8(demultiplexer_1_out8),
    .out9(demultiplexer_1_out9), .out10(demultiplexer_1_out10), .out11(demultiplexer_1_out11),
    .out12(demultiplexer_1_out12), .out13(demultiplexer_1_out13), .out14(demultiplexer_1_out14),
    .out15(demultiplexer_1_out15), .out16(demultiplexer_1_out16), .out17(demultiplexer_1_out17),
    .out18(demultiplexer_1_out18), .out19(demultiplexer_1_out19), .out20(demultiplexer_1_out20),
    .out21(demultiplexer_1_out21), .out22(demultiplexer_1_out22), .out23(demultiplexer_1_out23),
    .out24(demultiplexer_1_out24), .out25(demultiplexer_1_out25), .out26(demultiplexer_1_out26),
    .out27(demultiplexer_1_out27), .out28(demultiplexer_1_out28), .out29(demultiplexer_1_out29),
    .out30(demultiplexer_1_out30), .out31(demultiplexer_1_out31), .in(dmx_y_cord), .sel(dmx_x_cord));  // open: en
  Adder adder_1 (.a(register_1_q), .b(multiplexer_1_out), .out(adder_1_out));  // open: cin, cout
  Subtractor subtractor_1 (.a(register_1_q), .b(multiplexer_1_out), .out(subtractor_1_out));  // open: bin, bout
  Multiplexer #(.width(8)) multiplexer_2 (
    .in0(adder_1_out), .in1(subtractor_1_out), .out(multiplexer_2_out), .sel(register_2_q));  // open: en
  Register #(.width(1)) register_2 (.D(d_ff_1_q), .Q(register_2_q), .clk(power));  // open: en, clr
  Divider divider_1 (.a(multiplexer_2_out), .b(8'h8), .out(divider_1_out));  // open: upper, rem
  Bit_Extender #(.out_width(5)) bit_extender_1 (.in(divider_1_out), .out(dmx_x_cord));
  D_Flip_Flop d_ff_2 (.Q(isDown), .preset(dmx_y_cord[31]), .reset(dmx_y_cord[0]));  // open: clk, D, Qn, en
  Decoder #(.select(5)) decoder_1 (
    .out0(dmx_y_cord[0]), .out1(dmx_y_cord[1]), .out2(dmx_y_cord[2]), .out3(dmx_y_cord[3]),
    .out4(dmx_y_cord[4]), .out5(dmx_y_cord[5]), .out6(dmx_y_cord[6]), .out7(dmx_y_cord[7]),
    .out8(dmx_y_cord[8]), .out9(dmx_y_cord[9]), .out10(dmx_y_cord[10]), .out11(dmx_y_cord[11]),
    .out12(dmx_y_cord[12]), .out13(dmx_y_cord[13]), .out14(dmx_y_cord[14]), .out15(dmx_y_cord[15]),
    .out16(dmx_y_cord[16]), .out17(dmx_y_cord[17]), .out18(dmx_y_cord[18]), .out19(dmx_y_cord[19]),
    .out20(dmx_y_cord[20]), .out21(dmx_y_cord[21]), .out22(dmx_y_cord[22]), .out23(dmx_y_cord[23]),
    .out24(dmx_y_cord[24]), .out25(dmx_y_cord[25]), .out26(dmx_y_cord[26]), .out27(dmx_y_cord[27]),
    .out28(dmx_y_cord[28]), .out29(dmx_y_cord[29]), .out30(dmx_y_cord[30]), .out31(dmx_y_cord[31]),
    .sel(counter_1_q));  // open: en
  Counter #(.width(5), .max('h1f)) counter_1 (
    .load(isDown), .Q(counter_1_q), .clk(power));  // open: D, count, carry, clr
  Decoder #(.select(5)) decoder_2 (
    .out0(decoder_2_out0[0]), .out1(decoder_2_out0[1]), .out2(decoder_2_out0[2]), .out3(decoder_2_out0[3]),
    .out4(decoder_2_out0[4]), .out5(decoder_2_out0[5]), .out6(decoder_2_out0[6]), .out7(decoder_2_out0[7]),
    .out8(decoder_2_out0[8]), .out9(decoder_2_out0[9]), .out10(decoder_2_out0[10]),
    .out11(decoder_2_out0[11]), .out12(decoder_2_out0[12]), .out13(decoder_2_out0[13]),
    .out14(decoder_2_out0[14]), .out15(decoder_2_out0[15]), .out16(decoder_2_out0[16]),
    .out17(decoder_2_out0[17]), .out18(decoder_2_out0[18]), .out19(decoder_2_out0[19]),
    .out20(decoder_2_out0[20]), .out21(decoder_2_out0[21]), .out22(decoder_2_out0[22]),
    .out23(decoder_2_out0[23]), .out24(decoder_2_out0[24]), .out25(decoder_2_out0[25]),
    .out26(decoder_2_out0[26]), .out27(decoder_2_out0[27]), .out28(decoder_2_out0[28]),
    .out29(decoder_2_out0[29]), .out30(decoder_2_out0[30]), .out31(decoder_2_out0[31]), .sel(dmx_x_cord));  // open: en

  // Notes on the sheet:
  //   движение по оси x
  //   движение по оси y
endmodule
