// Logisim project numb.circ as structural Verilog: 1 circuit, main circuit main
module main (
);

  _7_Segment_Display u_7_segment_display_1 (.b(1'b1), .c(1'b1));  // open: g, f, a, e, d, dp
  _7_Segment_Display u_7_segment_display_2 (.g(1'b1), .a(1'b1), .b(1'b1), .e(1'b1), .d(1'b1));  // open: f, c, dp
  _7_Segment_Display u_7_segment_display_3 (.g(1'b1), .a(1'b1), .b(1'b1), .d(1'b1), .c(1'b1));  // open: f, e, dp
  _7_Segment_Display u_7_segment_display_4 (.g(1'b1), .f(1'b1), .b(1'b1), .c(1'b1));  // open: a, e, d, dp
  _7_Segment_Display u_7_segment_display_5 (.g(1'b1), .f(1'b1), .a(1'b1), .d(1'b1), .c(1'b1));  // open: b, e, dp
  _7_Segment_Display u_7_segment_display_6 (.g(1'b1), .f(1'b1), .a(1'b1), .e(1'b1), .d(1'b1), .c(1'b1));  // open: b, dp
  _7_Segment_Display u_7_segment_display_7 (.a(1'b1), .b(1'b1), .c(1'b1));  // open: g, f, e, d, dp
  _7_Segment_Display u_7_segment_display_8 (
    .g(1'b1), .f(1'b1), .a(1'b1), .b(1'b1), .e(1'b1), .d(1'b1), .c(1'b1));  // open: dp
  _7_Segment_Display u_7_segment_display_9 (.g(1'b1), .f(1'b1), .a(1'b1), .b(1'b1), .d(1'b1), .c(1'b1));  // open: e, dp
  _7_Segment_Display u_7_segment_display_10 (
    .f(1'b1), .a(1'b1), .b(1'b1), .e(1'b1), .d(1'b1), .c(1'b1));  // open: g, dp
endmodule
