// Logisim project numbers.circ as structural Verilog: 1 circuit, main circuit main
module main (
);

  wire [3:0] undriven, undriven_2;

  Hex_Digit_Display hex_digit_display_1 (.value(4'b0000));  // open: dp
  Hex_Digit_Display hex_digit_display_2 (.value(4'b0001));  // open: dp
  Hex_Digit_Display hex_digit_display_3 ();  // open: value, dp
  Hex_Digit_Display hex_digit_display_4 ();  // open: value, dp
  Hex_Digit_Display hex_digit_display_5 ();  // open: value, dp
  Hex_Digit_Display hex_digit_display_6 ();  // open: value, dp
  Hex_Digit_Display hex_digit_display_7 ();  // open: value, dp
  Hex_Digit_Display hex_digit_display_8 ();  // open: value, dp
  Hex_Digit_Display hex_digit_display_9 (.value(4'b0011));  // open: dp
  Hex_Digit_Display hex_digit_display_10 (.value(4'b0010));  // open: dp
  Hex_Digit_Display hex_digit_display_11 ();  // open: value, dp
  Hex_Digit_Display hex_digit_display_12 ();  // open: value, dp
  Hex_Digit_Display hex_digit_display_13 ();  // open: value, dp
  Hex_Digit_Display hex_digit_display_14 ();  // open: value, dp
  Hex_Digit_Display hex_digit_display_15 ();  // open: value, dp
  Hex_Digit_Display hex_digit_display_16 ();  // open: value, dp
  Hex_Digit_Display hex_digit_display_17 (.value(4'b0100));  // open: dp
  Hex_Digit_Display hex_digit_display_18 ();  // open: value, dp
  Hex_Digit_Display hex_digit_display_19 ();  // open: value, dp
  Hex_Digit_Display hex_digit_display_20 ();  // open: value, dp
  Hex_Digit_Display hex_digit_display_21 (.value(4'b0101));  // open: dp
  Hex_Digit_Display hex_digit_display_22 (.value(4'b0110));  // open: dp
  Hex_Digit_Display hex_digit_display_23 ();  // open: value, dp
  Hex_Digit_Display hex_digit_display_24 ();  // open: value, dp
  Hex_Digit_Display hex_digit_display_25 ();  // open: value, dp
  Hex_Digit_Display hex_digit_display_26 ();  // open: value, dp
  Hex_Digit_Display hex_digit_display_27 ();  // open: value, dp
  Hex_Digit_Display hex_digit_display_28 ();  // open: value, dp
  Hex_Digit_Display hex_digit_display_29 (.value(4'b0111));  // open: dp
  Hex_Digit_Display hex_digit_display_30 ();  // open: value, dp
  Hex_Digit_Display hex_digit_display_31 ();  // open: value, dp
  Hex_Digit_Display hex_digit_display_32 ();  // open: value, dp
  Hex_Digit_Display hex_digit_display_33 (.value(4'b1001));  // open: dp
  Hex_Digit_Display hex_digit_display_34 (.value(4'b1000));  // open: dp
  Hex_Digit_Display hex_digit_display_35 ();  // open: value, dp
  Hex_Digit_Display hex_digit_display_36 ();  // open: value, dp
  Hex_Digit_Display hex_digit_display_37 ();  // open: value, dp
  Hex_Digit_Display hex_digit_display_38 ();  // open: value, dp
  Hex_Digit_Display hex_digit_display_39 ();  // open: value, dp
  Hex_Digit_Display hex_digit_display_40 ();  // open: value, dp
  Hex_Digit_Display hex_digit_display_41 (.value(undriven_2));  // open: dp
  Hex_Digit_Display hex_digit_display_42 (.value(undriven));  // open: dp
  Hex_Digit_Display hex_digit_display_43 ();  // open: value, dp
  Hex_Digit_Display hex_digit_display_44 ();  // open: value, dp
  Hex_Digit_Display hex_digit_display_45 ();  // open: value, dp
  Hex_Digit_Display hex_digit_display_46 ();  // open: value, dp
  Hex_Digit_Display hex_digit_display_47 ();  // open: value, dp
  Hex_Digit_Display hex_digit_display_48 ();  // open: value, dp
  Hex_Digit_Display hex_digit_display_49 ();  // open: value, dp
  Hex_Digit_Display hex_digit_display_50 ();  // open: value, dp
  Hex_Digit_Display hex_digit_display_51 ();  // open: value, dp
  Hex_Digit_Display hex_digit_display_52 ();  // open: value, dp
  Hex_Digit_Display hex_digit_display_53 ();  // open: value, dp
  Hex_Digit_Display hex_digit_display_54 ();  // open: value, dp
  Hex_Digit_Display hex_digit_display_55 ();  // open: value, dp
  Hex_Digit_Display hex_digit_display_56 ();  // open: value, dp
  Hex_Digit_Display hex_digit_display_57 ();  // open: value, dp
  Hex_Digit_Display hex_digit_display_58 ();  // open: value, dp
  Hex_Digit_Display hex_digit_display_59 ();  // open: value, dp
  Hex_Digit_Display hex_digit_display_60 ();  // open: value, dp
  Hex_Digit_Display hex_digit_display_61 ();  // open: value, dp
  Hex_Digit_Display hex_digit_display_62 ();  // open: value, dp
  Hex_Digit_Display hex_digit_display_63 ();  // open: value, dp
  Hex_Digit_Display hex_digit_display_64 ();  // open: value, dp
endmodule
