// Logisim project ping-pong.circ as structural Verilog: 16 circuits, main circuit movePoint
module movePoint (
  input  [6:0] Keyboard,
  output [3:0] out_2,
  output [3:0] out_3,
  output [3:0] out_4,
  output [31:0] out_5,
  output [31:0] out_6,
  output [31:0] out_7,
  output [31:0] out_8,
  output [31:0] out_9,
  output [31:0] out_10,
  output [31:0] out_11,
  output [31:0] out_12,
  output [31:0] out_13,
  output [31:0] out_14,
  output [31:0] out_15,
  output [31:0] out_16,
  output [31:0] out_17,
  output [31:0] out_18,
  output [31:0] out_19,
  output [31:0] out_20,
  output [31:0] out_21,
  output [31:0] out_22,
  output [31:0] out_23,
  output [31:0] out_24,
  output [31:0] out_25,
  output [31:0] out_26,
  output [31:0] out_27,
  output [31:0] out_28,
  output [31:0] out_29,
  output [31:0] out_30,
  output [31:0] out_31,
  output [31:0] out_32,
  output [31:0] out_33,
  output [31:0] out_34,
  output [31:0] out_35,
  output [31:0] out_36,
  output [3:0] out_37,
  output [3:0] out_38,
  output [3:0] out_39,
  output [3:0] sec_0,
  output [3:0] sec_1,
  output [3:0] min_0,
  output [3:0] min_1,
  output keyboard_power
);

  wire and_1_out, and_2_out, and_4_out, and_5_out, and_6_out, and_7_out, and_8_out, and_9_out, and_10_out,
       and_11_out, and_12_out, and_13_out, and_14_out, and_15_out, b_button, b_pressed, bot_down,
       bot_enabled, comparator_2_eq, comparator_7_eq, comparator_8_eq, comparator_9_gt, comparator_10_lt,
       comparator_11_eq, comparator_12_eq, comparator_13_eq, comparator_14_eq, comparator_15_eq,
       comparator_16_eq, comparator_17_eq, comparator_18_eq, comparator_19_eq, comparator_21_eq, d_ff_2_q,
       enable_move, fail1, fail2, frequency_divider_1_out, frequency_divider_3_out, frequency_divider_4_out,
       gameover, is_ball_16, isDown, isLeft, L_button, l_button_t, l_pressed, not_1_out, not_2_out,
       not_3_out, not_4_out, not_5_out, not_6_out, not_7_out, not_8_out, not_9_out, not_10_out, not_11_out,
       not_12_out, not_13_out, not_14_out, not_15_out, not_16_out, not_17_out, not_18_out, not_19_out,
       not_20_out, not_21_out, not_22_out, not_23_out, not_24_out, not_25_out, not_26_out, not_27_out,
       not_28_out, not_29_out, not_30_out, o_button, o_pressed, or_6_out, or_7_out, or_11_out, or_12_out,
       or_13_out, or_14_out, or_16_out, or_17_out, or_18_out, or_19_out, or_22_out, or_23_out, or_24_out,
       or_26_out, or_27_out, or_28_out, or_30_out, or_31_out, or_32_out, P, pause, playing, power,
       pull_resistor_1_node, pull_resistor_2_node, pull_resistor_3_node, r1, r2, rest_pressed, restart,
       s_button, s_pressed, space_on, space_pr, space_pressed, swap_x_dir_left_r_to_left,
       swap_x_dir_right_r_to_right, swap_x_direction_left_wall, swap_x_direction_right_wall, t_ff_1_q,
       transistor_3_out, transistor_5_out, transistor_6_out, transistor_7_out, w_button, w_pressed, win;
  wire [2:0] aoa;
  wire [3:0] bit_extender_1_out;
  wire [4:0] counter_1_q, counter_2_q, dmx_x_cord_L, dmx_x_cord_R, middle_rocket_pixel_left,
       multiplexer_120_out, prev_val, register_2_q;
  wire [4:4] undriven;
  wire [5:0] counter_6_q, dmx_x_cord, multiplexer_122_out;
  wire [6:0] keyboard_t, test_keyboard;
  wire [7:0] bit_extender_2_out, bit_extender_3_out, bot_borris_1_new_y, multiplexer_109_out,
       multiplexer_110_out, multiplexer_118_out, p1_score_bin, p2_score_bin, x_speed, y_speed;
  wire [15:0] S4, S5, S7, S9, S10, S12, S14, S15, S17, S19, S20, S22, S24, S25, S27;
  wire [29:2] decoder_2_out0, middle_rocket_pixel_right;
  wire [31:0] adder_1_out, bot, cord1, cord2, cord11, cord22, D0, D1, D3, D5, D6, D7, D8, D9, D10, D11, D12,
       D13, D14, D15, D16, D17, D18, D19, D20, D21, D22, D23, D24, D25, D26, D27, D28, D29, D30, D31, D32,
       D33, D34, D35, D36, D37, D38, D39, D40, D41, D42, D43, D44, D45, D46, D47, D48, D49, D50, D51, D52,
       D53, D54, D55, D56, D57, D58, D60, D62, D63, demultiplexer_1_out3, demultiplexer_2_out28, dmx_y_cord,
       lw4, lw5, lw6, lw7, lw8, lw9, lw10, lw11, lw12, lw13, lw14, lw15, multiplexer_25_out,
       multiplexer_41_out, multiplexer_58_out, multiplexer_75_out, multiplexer_108_out, multiplexer_112_out,
       multiplexer_113_out, multiplexer_114_out, multiplexer_116_out, multiplexer_117_out,
       multiplexer_119_out, n32, n33, n34, n35, n36, n37, n38, n39, n40, n41, n42, n43, n44, n45, n46, n47,
       n48, n49, n50, n51, n52, n53, n54, n55, n56, n57, n58, n59, n60, n61, n62, n63, p30, p33, player1,
       player2, racket2, register_1_q, shifter_1_out, shifter_2_out, shifter_3_out, shifter_4_out,
       shifter_5_out, shifter_6_out, shifter_7_out, shifter_8_out, shifter_9_out, shifter_10_out,
       shifter_11_out, shifter_12_out, shifter_13_out, shifter_14_out, whereMoveBot, wl36, wl37, wl38, wl39,
       wl40, wl41, wl42, wl43, wl44, wl45, wl46, wl47, y_pause_cord;

  Multiplexer #(.width(32)) multiplexer_1 (.in0({32{1'b0}}), .in1(32'h60000), .out(lw4), .sel(win));  // open: en
  Multiplexer #(.width(32)) multiplexer_2 (.in0({32{1'b0}}), .in1(32'h90000), .out(lw5), .sel(win));  // open: en
  Multiplexer #(.width(32)) multiplexer_3 (.in0({32{1'b0}}), .in1(32'h9c000), .out(lw6), .sel(win));  // open: en
  Multiplexer #(.width(32)) multiplexer_4 (.in0({32{1'b0}}), .in1(32'h63000), .out(lw7), .sel(win));  // open: en
  Multiplexer #(.width(32)) multiplexer_5 (.in0(32'h7c000), .in1(32'h10c00), .out(lw8), .sel(win));  // open: en
  Multiplexer #(.width(32)) multiplexer_6 (.in0(32'h382000), .in1(32'h10200), .out(lw9), .sel(win));  // open: en
  Multiplexer #(.width(32)) multiplexer_7 (.in0(32'h439000), .in1(32'h8200), .out(lw10), .sel(win));  // open: en
  Multiplexer #(.width(32)) multiplexer_8 (.in0(32'h87d000), .in1(32'h8200), .out(lw11), .sel(win));  // open: en
  Multiplexer #(.width(32)) multiplexer_9 (.in0(32'h87cf00), .in1(32'h4200), .out(lw12), .sel(win));  // open: en
  Multiplexer #(.width(32)) multiplexer_10 (.in0(32'h107c080), .in1(32'h18200), .out(lw13), .sel(win));  // open: en
  Multiplexer #(.width(32)) multiplexer_11 (.in0(32'h1038080), .in1(32'h360200), .out(lw14), .sel(win));  // open: en
  Multiplexer #(.width(32)) multiplexer_12 (.in0(32'h1001880), .in1(32'h480200), .out(lw15), .sel(win));  // open: en
  Multiplexer #(.width(32), .disabled(0)) multiplexer_13 (
    .in0({32{1'b0}}), .in1(32'h60000), .out(wl36), .sel(not_1_out));  // open: en
  not not_1 (not_1_out, win);
  Multiplexer #(.width(32)) multiplexer_14 (
    .in0({32{1'b0}}), .in1(32'h90000), .out(wl37), .sel(not_2_out));  // open: en
  not not_2 (not_2_out, win);
  Multiplexer #(.width(32)) multiplexer_15 (
    .in0({32{1'b0}}), .in1(32'h9c000), .out(wl38), .sel(not_3_out));  // open: en
  not not_3 (not_3_out, win);
  Multiplexer #(.width(32)) multiplexer_16 (
    .in0({32{1'b0}}), .in1(32'h63000), .out(wl39), .sel(not_4_out));  // open: en
  not not_4 (not_4_out, win);
  Multiplexer #(.width(32)) multiplexer_17 (.in0(32'h7c000), .in1(32'h10c00), .out(wl40), .sel(not_5_out));  // open: en
  not not_5 (not_5_out, win);
  Multiplexer #(.width(32)) multiplexer_18 (
    .in0(32'h382000), .in1(32'h10200), .out(wl41), .sel(not_6_out));  // open: en
  not not_6 (not_6_out, win);
  Multiplexer #(.width(32)) multiplexer_19 (.in0(32'h439000), .in1(32'h8200), .out(wl42), .sel(not_7_out));  // open: en
  not not_7 (not_7_out, win);
  Multiplexer #(.width(32)) multiplexer_20 (.in0(32'h87d000), .in1(32'h8200), .out(wl43), .sel(not_8_out));  // open: en
  not not_8 (not_8_out, win);
  Multiplexer #(.width(32)) multiplexer_21 (.in0(32'h87cf00), .in1(32'h4200), .out(wl44), .sel(not_9_out));  // open: en
  not not_9 (not_9_out, win);
  Multiplexer #(.width(32)) multiplexer_22 (
    .in0(32'h107c080), .in1(32'h18200), .out(wl45), .sel(not_10_out));  // open: en
  not not_10 (not_10_out, win);
  Multiplexer #(.width(32)) multiplexer_23 (
    .in0(32'h1038080), .in1(32'h360200), .out(wl46), .sel(not_11_out));  // open: en
  not not_11 (not_11_out, win);
  Multiplexer #(.width(32)) multiplexer_24 (
    .in0(32'h1001880), .in1(32'h480200), .out(wl47), .sel(not_12_out));  // open: en
  not not_12 (not_12_out, win);
  DotMatrix #(.matrixcols(1), .matrixrows(32)) dotmatrix_1 (.col0(multiplexer_25_out));
  Multiplexer #(.width(32)) multiplexer_25 (
    .in0({32{1'b0}}), .in1({32{1'b1}}), .out(multiplexer_25_out), .sel(pull_resistor_1_node));  // open: en
  Pull_Resistor pull_resistor_1 (.node(pull_resistor_1_node));
  Transistor #(.\type ("n"), .gate("br")) transistor_1 (.in(fail1), .out(pull_resistor_1_node), .gate(playing));
  assign bit_extender_1_out = {{1{1'b0}}, aoa};  // Bit_Extender bit_extender_1
  // Probe on 11'h330
  frequency_divider_11bit frequency_divider_11bit_1 (.IN(keyboard_power), .n(11'h330), .OUT(space_on));  // open: _0
  Multiplexer #(.width(16)) multiplexer_26 (.in0({16{1'b0}}), .in1(16'h3200), .out(S4), .sel(space_on));  // open: en
  Multiplexer #(.width(16)) multiplexer_27 (.in0({16{1'b0}}), .in1(16'h7f00), .out(S9), .sel(space_on));  // open: en
  Multiplexer #(.width(16)) multiplexer_28 (.in0({16{1'b0}}), .in1(16'h3f00), .out(S14), .sel(space_on));  // open: en
  Multiplexer #(.width(16)) multiplexer_29 (.in0({16{1'b0}}), .in1(16'h3e00), .out(S19), .sel(space_on));  // open: en
  Multiplexer #(.width(16)) multiplexer_30 (.in0({16{1'b0}}), .in1(16'h7f00), .out(S24), .sel(space_on));  // open: en
  DotMatrix #(.matrixcols(32), .matrixrows(32)) dotmatrix_2 (
    .col0(out_5), .col1(out_6), .col2(out_7), .col3(out_8), .col4(out_9), .col5(out_10), .col6(out_11),
    .col7(out_12), .col8(out_13), .col9(out_14), .col10(out_15), .col11(out_16), .col12(out_17),
    .col13(out_18), .col14(out_19), .col15(out_20), .col16(out_21), .col17(out_22), .col18(out_23),
    .col19(out_24), .col20(out_25), .col21(out_26), .col22(out_27), .col23(out_28), .col24(out_29),
    .col25(out_30), .col26(out_31), .col27(out_32), .col28(out_33), .col29(out_34), .col30(out_35),
    .col31(out_36));
  // Probe on dmx_x_cord
  Hex_Digit_Display hex_digit_display_1 (.value(bit_extender_1_out));  // open: dp
  Multiplexer #(.width(16)) multiplexer_31 (.in0({16{1'b0}}), .in1(16'h4900), .out(S5), .sel(space_on));  // open: en
  Multiplexer #(.width(16)) multiplexer_32 (.in0({16{1'b0}}), .in1(16'h4800), .out(S10), .sel(space_on));  // open: en
  Multiplexer #(.width(16)) multiplexer_33 (.in0({16{1'b0}}), .in1(16'h4400), .out(S15), .sel(space_on));  // open: en
  Multiplexer #(.width(16)) multiplexer_34 (.in0({16{1'b0}}), .in1(16'h4100), .out(S20), .sel(space_on));  // open: en
  Multiplexer #(.width(16)) multiplexer_35 (.in0({16{1'b0}}), .in1(16'h4900), .out(S25), .sel(space_on));  // open: en
  Hex_Digit_Display hex_digit_display_2 (.value(out_2));  // open: dp
  Hex_Digit_Display hex_digit_display_3 (.value(out_3));  // open: dp
  assign D3 = player1 | demultiplexer_1_out3;  // OR_Gate or_1, 32 bits wide
  Multiplexer #(.width(16)) multiplexer_36 (.in0({16{1'b0}}), .in1(16'h2600), .out(S7), .sel(space_on));  // open: en
  Multiplexer #(.width(16)) multiplexer_37 (.in0({16{1'b0}}), .in1(16'h3000), .out(S12), .sel(space_on));  // open: en
  Multiplexer #(.width(16)) multiplexer_38 (.in0({16{1'b0}}), .in1(16'h3f00), .out(S17), .sel(space_on));  // open: en
  Multiplexer #(.width(16)) multiplexer_39 (.in0({16{1'b0}}), .in1(16'h4100), .out(S22), .sel(space_on));  // open: en
  Multiplexer #(.width(16)) multiplexer_40 (.in0({16{1'b0}}), .in1(16'h4900), .out(S27), .sel(space_on));  // open: en
  Hex_Digit_Display hex_digit_display_4 (.value(out_4));  // open: dp
  Keyboard #(.buflen(1)) keyboard_1 (.clk(keyboard_power), .data(test_keyboard));  // open: re, clr, avail
  Demultiplexer #(.select(5), .width(32)) demultiplexer_1 (
    .out0(D0), .out1(D1), .out2(cord11), .out3(demultiplexer_1_out3), .out4(cord1), .out5(D5), .out6(D6),
    .out7(D7), .out8(D8), .out9(D9), .out10(D10), .out11(D11), .out12(D12), .out13(D13), .out14(D14),
    .out15(D15), .out16(D16), .out17(D17), .out18(D18), .out19(D19), .out20(D20), .out21(D21), .out22(D22),
    .out23(D23), .out24(D24), .out25(D25), .out26(D26), .out27(D27), .out28(D28), .out29(D29), .out30(D30),
    .out31(D31), .in(multiplexer_41_out), .sel(dmx_x_cord_L));  // open: en
  Multiplexer #(.width(32)) multiplexer_41 (
    .in0(dmx_y_cord), .in1({32{1'b0}}), .out(multiplexer_41_out), .sel(dmx_x_cord[5]));  // open: en
  DotMatrix #(.matrixcols(32), .matrixrows(32)) dotmatrix_3 (
    .col0(n32), .col1(n33), .col2(n34), .col3(n35), .col4(n36), .col5(n37), .col6(n38), .col7(n39),
    .col8(n40), .col9(n41), .col10(n42), .col11(n43), .col12(n44), .col13(n45), .col14(n46), .col15(n47),
    .col16(n48), .col17(n49), .col18(n50), .col19(n51), .col20(n52), .col21(n53), .col22(n54), .col23(n55),
    .col24(n56), .col25(n57), .col26(n58), .col27(n59), .col28(n60), .col29(n61), .col30(n62), .col31(n63));
  assign p30 = y_pause_cord | D30;  // OR_Gate or_2, 32 bits wide
  assign p33 = y_pause_cord | D33;  // OR_Gate or_3, 32 bits wide
  Hex_Digit_Display hex_digit_display_5 (.value(out_38));  // open: dp
  Hex_Digit_Display hex_digit_display_6 (.value(out_37));  // open: dp
  Hex_Digit_Display hex_digit_display_7 (.value(out_39));  // open: dp
  Multiplexer #(.select(2), .width(32), .enable("false")) multiplexer_42 (
    .in0({32{1'b0}}), .in1(D0), .in2({32{1'b0}}), .in3(D0), .out(out_5), .sel({pause, playing}));
  Multiplexer #(.select(2), .width(32), .enable("false")) multiplexer_43 (
    .in0({32{1'b0}}), .in1(cord1), .in2(lw4), .in3(cord1), .out(out_9), .sel({pause, playing}));
  Multiplexer #(.select(2), .width(32), .enable("false")) multiplexer_44 (
    .in0({32{1'b0}}), .in1(D8), .in2(lw8), .in3(D8), .out(out_13), .sel({pause, playing}));
  Multiplexer #(.select(2), .width(32), .enable("false")) multiplexer_45 (
    .in0({32{1'b0}}), .in1(D12), .in2(lw12), .in3(D12), .out(out_17), .sel({pause, playing}));
  Multiplexer #(.select(2), .width(32), .enable("false")) multiplexer_46 (
    .in0({32{1'b0}}), .in1(D16), .in2(lw15), .in3(D16), .out(out_21), .sel({pause, playing}));
  Multiplexer #(.select(2), .width(32), .enable("false")) multiplexer_47 (
    .in0({16'hfe, S4}), .in1(D20), .in2(lw11), .in3(D20), .out(out_25), .sel({pause, playing}));
  Multiplexer #(.select(2), .width(32), .enable("false")) multiplexer_48 (
    .in0({32{1'b0}}), .in1(D24), .in2(lw7), .in3(D24), .out(out_29), .sel({pause, playing}));
  Multiplexer #(.select(2), .width(32), .enable("false")) multiplexer_49 (
    .in0({16'h6e, S12}), .in1(D28), .in2({32{1'b0}}), .in3(D28), .out(out_33), .sel({pause, playing}));
  Multiplexer #(.select(2), .width(32), .enable("false")) multiplexer_50 (
    .in0({16'h92, S15}), .in1(D32), .in2({32{1'b0}}), .in3(D32), .out(n32), .sel({pause, playing}));
  Multiplexer #(.select(2), .width(32), .enable("false")) multiplexer_51 (
    .in0({16'h92, S20}), .in1(D36), .in2(wl36), .in3(D36), .out(n36), .sel({pause, playing}));
  Multiplexer #(.select(2), .width(32), .enable("false")) multiplexer_52 (
    .in0({16'h64, S24}), .in1(D40), .in2(wl40), .in3(D40), .out(n40), .sel({pause, playing}));
  Multiplexer #(.select(2), .width(32), .enable("false")) multiplexer_53 (
    .in0({32{1'b0}}), .in1(D44), .in2(wl44), .in3(D44), .out(n44), .sel({pause, playing}));
  Multiplexer #(.select(2), .width(32), .enable("false")) multiplexer_54 (
    .in0({32{1'b0}}), .in1(D48), .in2(wl47), .in3(D48), .out(n48), .sel({pause, playing}));
  Multiplexer #(.select(2), .width(32), .enable("false")) multiplexer_55 (
    .in0({32{1'b0}}), .in1(D52), .in2(wl43), .in3(D52), .out(n52), .sel({pause, playing}));
  Multiplexer #(.select(2), .width(32), .enable("false")) multiplexer_56 (
    .in0({32{1'b0}}), .in1(D56), .in2(wl39), .in3(D56), .out(n56), .sel({pause, playing}));
  Multiplexer #(.select(2), .width(32), .enable("false")) multiplexer_57 (
    .in0({32{1'b0}}), .in1(D60), .in2({32{1'b0}}), .in3(D60), .out(n60), .sel({pause, playing}));
  // Probe on bot
  assign keyboard_t = test_keyboard | Keyboard;  // OR_Gate or_4, 7 bits wide
  DotMatrix #(.matrixcols(1), .matrixrows(32)) dotmatrix_4 (.col0(multiplexer_58_out));
  Multiplexer #(.width(32)) multiplexer_58 (
    .in0({32{1'b0}}), .in1({32{1'b1}}), .out(multiplexer_58_out), .sel(pull_resistor_2_node));  // open: en
  Pull_Resistor pull_resistor_2 (.node(pull_resistor_2_node));
  Multiplexer #(.select(2), .width(32), .enable("false")) multiplexer_59 (
    .in0({32{1'b0}}), .in1(D1), .in2({32{1'b0}}), .in3(D1), .out(out_6), .sel({pause, playing}));
  Multiplexer #(.select(2), .width(32), .enable("false")) multiplexer_60 (
    .in0({32{1'b0}}), .in1(D5), .in2(lw5), .in3(D5), .out(out_10), .sel({pause, playing}));
  Multiplexer #(.select(2), .width(32), .enable("false")) multiplexer_61 (
    .in0({32{1'b0}}), .in1(D9), .in2(lw9), .in3(D9), .out(out_14), .sel({pause, playing}));
  Multiplexer #(.select(2), .width(32), .enable("false")) multiplexer_62 (
    .in0({32{1'b0}}), .in1(D13), .in2(lw13), .in3(D13), .out(out_18), .sel({pause, playing}));
  Multiplexer #(.select(2), .width(32), .enable("false")) multiplexer_63 (
    .in0({32{1'b0}}), .in1(D17), .in2(lw14), .in3(D17), .out(out_22), .sel({pause, playing}));
  Multiplexer #(.select(2), .width(32), .enable("false")) multiplexer_64 (
    .in0({16'h90, S5}), .in1(D21), .in2(lw10), .in3(D21), .out(out_26), .sel({pause, playing}));
  Multiplexer #(.select(2), .width(32), .enable("false")) multiplexer_65 (
    .in0({16'hfe, S9}), .in1(D25), .in2(lw6), .in3(D25), .out(out_30), .sel({pause, playing}));
  Multiplexer #(.select(2), .width(32), .enable("false")) multiplexer_66 (
    .in0({32{1'b0}}), .in1(D29), .in2({32{1'b0}}), .in3(D29), .out(out_34), .sel({pause, playing}));
  Multiplexer #(.select(2), .width(32), .enable("false")) multiplexer_67 (
    .in0({16'h92, S17}), .in1(D33), .in2({32{1'b0}}), .in3(p33), .out(n33), .sel({pause, playing}));
  Multiplexer #(.select(2), .width(32), .enable("false")) multiplexer_68 (
    .in0({16'h92, S20}), .in1(D37), .in2(wl37), .in3(D37), .out(n37), .sel({pause, playing}));
  Multiplexer #(.select(2), .width(32), .enable("false")) multiplexer_69 (
    .in0({16'h92, S25}), .in1(D41), .in2(wl41), .in3(D41), .out(n41), .sel({pause, playing}));
  Multiplexer #(.select(2), .width(32), .enable("false")) multiplexer_70 (
    .in0({32{1'b0}}), .in1(D45), .in2(wl45), .in3(D45), .out(n45), .sel({pause, playing}));
  Multiplexer #(.select(2), .width(32), .enable("false")) multiplexer_71 (
    .in0({32{1'b0}}), .in1(D49), .in2(wl46), .in3(D49), .out(n49), .sel({pause, playing}));
  Multiplexer #(.select(2), .width(32), .enable("false")) multiplexer_72 (
    .in0({32{1'b0}}), .in1(D53), .in2(wl42), .in3(D53), .out(n53), .sel({pause, playing}));
  Multiplexer #(.select(2), .width(32), .enable("false")) multiplexer_73 (
    .in0({32{1'b0}}), .in1(D57), .in2(wl38), .in3(D57), .out(n57), .sel({pause, playing}));
  Multiplexer #(.select(2), .width(32), .enable("false")) multiplexer_74 (
    .in0({32{1'b0}}), .in1(cord22), .in2({32{1'b0}}), .in3(cord22), .out(n61), .sel({pause, playing}));
  Transistor #(.\type ("n"), .gate("br")) transistor_2 (.in(fail2), .out(pull_resistor_2_node), .gate(playing));
  Demultiplexer #(.select(5), .width(32)) demultiplexer_2 (
    .out0(D32), .out1(D33), .out2(D34), .out3(D35), .out4(D36), .out5(D37), .out6(D38), .out7(D39),
    .out8(D40), .out9(D41), .out10(D42), .out11(D43), .out12(D44), .out13(D45), .out14(D46), .out15(D47),
    .out16(D48), .out17(D49), .out18(D50), .out19(D51), .out20(D52), .out21(D53), .out22(D54), .out23(D55),
    .out24(D56), .out25(D57), .out26(D58), .out27(cord2), .out28(demultiplexer_2_out28), .out29(cord22),
    .out30(D62), .out31(D63), .in(multiplexer_75_out), .sel(dmx_x_cord_R));  // open: en
  Multiplexer #(.width(32)) multiplexer_75 (
    .in0({32{1'b0}}), .in1(dmx_y_cord), .out(multiplexer_75_out), .sel(dmx_x_cord[5]));  // open: en
  Transistor transistor_3 (.in(playing), .out(transistor_3_out), .gate(pause));
  Multiplexer #(.select(2), .width(32), .enable("false")) multiplexer_76 (
    .in0({32{1'b0}}), .in1(cord11), .in2({32{1'b0}}), .in3(cord11), .out(out_7), .sel({pause, playing}));
  Multiplexer #(.select(2), .width(32), .enable("false")) multiplexer_77 (
    .in0({32{1'b0}}), .in1(D6), .in2(lw6), .in3(D6), .out(out_11), .sel({pause, playing}));
  Multiplexer #(.select(2), .width(32), .enable("false")) multiplexer_78 (
    .in0({32{1'b0}}), .in1(D10), .in2(lw10), .in3(D10), .out(out_15), .sel({pause, playing}));
  Multiplexer #(.select(2), .width(32), .enable("false")) multiplexer_79 (
    .in0({32{1'b0}}), .in1(D14), .in2(lw14), .in3(D14), .out(out_19), .sel({pause, playing}));
  Multiplexer #(.select(2), .width(32), .enable("false")) multiplexer_80 (
    .in0({32{1'b0}}), .in1(D18), .in2(lw13), .in3(D18), .out(out_23), .sel({pause, playing}));
  Multiplexer #(.select(2), .width(32), .enable("false")) multiplexer_81 (
    .in0({16'h90, S5}), .in1(D22), .in2(lw9), .in3(D22), .out(out_27), .sel({pause, playing}));
  Multiplexer #(.select(2), .width(32), .enable("false")) multiplexer_82 (
    .in0({16'h90, S10}), .in1(D26), .in2(lw5), .in3(D26), .out(out_31), .sel({pause, playing}));
  Multiplexer #(.select(2), .width(32), .enable("false")) multiplexer_83 (
    .in0({16'hfe, S14}), .in1(D30), .in2({32{1'b0}}), .in3(p30), .out(out_35), .sel({pause, playing}));
  Multiplexer #(.select(2), .width(32), .enable("false")) multiplexer_84 (
    .in0({32{1'b0}}), .in1(D34), .in2({32{1'b0}}), .in3(D34), .out(n34), .sel({pause, playing}));
  Multiplexer #(.select(2), .width(32), .enable("false")) multiplexer_85 (
    .in0({16'h4c, S22}), .in1(D38), .in2(wl38), .in3(D38), .out(n38), .sel({pause, playing}));
  Multiplexer #(.select(2), .width(32), .enable("false")) multiplexer_86 (
    .in0({16'h92, S25}), .in1(D42), .in2(wl42), .in3(D42), .out(n42), .sel({pause, playing}));
  Multiplexer #(.select(2), .width(32), .enable("false")) multiplexer_87 (
    .in0({32{1'b0}}), .in1(D46), .in2(wl46), .in3(D46), .out(n46), .sel({pause, playing}));
  Multiplexer #(.select(2), .width(32), .enable("false")) multiplexer_88 (
    .in0({32{1'b0}}), .in1(D50), .in2(wl45), .in3(D50), .out(n50), .sel({pause, playing}));
  Multiplexer #(.select(2), .width(32), .enable("false")) multiplexer_89 (
    .in0({32{1'b0}}), .in1(D54), .in2(wl41), .in3(D54), .out(n54), .sel({pause, playing}));
  Multiplexer #(.select(2), .width(32), .enable("false")) multiplexer_90 (
    .in0({32{1'b0}}), .in1(D58), .in2(wl37), .in3(D58), .out(n58), .sel({pause, playing}));
  Multiplexer #(.select(2), .width(32), .enable("false")) multiplexer_91 (
    .in0({32{1'b0}}), .in1(D62), .in2({32{1'b0}}), .in3(D62), .out(n62), .sel({pause, playing}));
  assign D60 = racket2 | demultiplexer_2_out28;  // OR_Gate or_5, 32 bits wide
  or or_6 (or_6_out, restart, gameover);
  stopWatch2hz stopwatch2hz_1 (
    .start(transistor_3_out), .takt(keyboard_power), .\null (or_6_out), .min_1(min_1), .min_0(min_0),
    .sec_1(sec_1), .sec_0(sec_0));
  Multiplexer #(.select(2), .width(32), .enable("false")) multiplexer_92 (
    .in0({32{1'b0}}), .in1(D3), .in2({32{1'b0}}), .in3(D3), .out(out_8), .sel({pause, playing}));
  Multiplexer #(.select(2), .width(32), .enable("false")) multiplexer_93 (
    .in0({32{1'b0}}), .in1(D7), .in2(lw7), .in3(D7), .out(out_12), .sel({pause, playing}));
  Multiplexer #(.select(2), .width(32), .enable("false")) multiplexer_94 (
    .in0({32{1'b0}}), .in1(D11), .in2(lw11), .in3(D11), .out(out_16), .sel({pause, playing}));
  Multiplexer #(.select(2), .width(32), .enable("false")) multiplexer_95 (
    .in0({32{1'b0}}), .in1(D15), .in2(lw15), .in3(D15), .out(out_20), .sel({pause, playing}));
  Multiplexer #(.select(2), .width(32), .enable("false")) multiplexer_96 (
    .in0({32{1'b0}}), .in1(D19), .in2(lw12), .in3(D19), .out(out_24), .sel({pause, playing}));
  Multiplexer #(.select(2), .width(32), .enable("false")) multiplexer_97 (
    .in0({16'h60, S7}), .in1(D23), .in2(lw8), .in3(D23), .out(out_28), .sel({pause, playing}));
  Multiplexer #(.select(2), .width(32), .enable("false")) multiplexer_98 (
    .in0({16'h90, S10}), .in1(D27), .in2(lw4), .in3(D27), .out(out_32), .sel({pause, playing}));
  Multiplexer #(.select(2), .width(32), .enable("false")) multiplexer_99 (
    .in0({16'h92, S15}), .in1(D31), .in2({32{1'b0}}), .in3(D31), .out(out_36), .sel({pause, playing}));
  Multiplexer #(.select(2), .width(32), .enable("false")) multiplexer_100 (
    .in0({16'h64, S19}), .in1(D35), .in2({32{1'b0}}), .in3(D35), .out(n35), .sel({pause, playing}));
  Multiplexer #(.select(2), .width(32), .enable("false")) multiplexer_101 (
    .in0({32{1'b0}}), .in1(D39), .in2(wl39), .in3(D39), .out(n39), .sel({pause, playing}));
  Multiplexer #(.select(2), .width(32), .enable("false")) multiplexer_102 (
    .in0({16'h4c, S27}), .in1(D43), .in2(wl43), .in3(D43), .out(n43), .sel({pause, playing}));
  Multiplexer #(.select(2), .width(32), .enable("false")) multiplexer_103 (
    .in0({32{1'b0}}), .in1(D47), .in2(wl47), .in3(D47), .out(n47), .sel({pause, playing}));
  Multiplexer #(.select(2), .width(32), .enable("false")) multiplexer_104 (
    .in0({32{1'b0}}), .in1(D51), .in2(wl44), .in3(D51), .out(n51), .sel({pause, playing}));
  Multiplexer #(.select(2), .width(32), .enable("false")) multiplexer_105 (
    .in0({32{1'b0}}), .in1(D55), .in2(wl40), .in3(D55), .out(n55), .sel({pause, playing}));
  Multiplexer #(.select(2), .width(32), .enable("false")) multiplexer_106 (
    .in0({32{1'b0}}), .in1(cord2), .in2(wl36), .in3(cord2), .out(n59), .sel({pause, playing}));
  Multiplexer #(.select(2), .width(32), .enable("false")) multiplexer_107 (
    .in0({32{1'b0}}), .in1(D63), .in2({32{1'b0}}), .in3(D63), .out(n63), .sel({pause, playing}));
  // Probe on racket2
  // Probe on player1
  // Probe on {2'b00, middle_rocket_pixel_right, 2'b00}
  Pull_Resistor pull_resistor_3 (.node(pull_resistor_3_node));
  Register #(.width(32)) register_1 (
    .D(multiplexer_108_out), .Q(register_1_q), .clk(or_7_out), .clr(not_13_out));  // open: en
  Multiplexer #(.width(32)) multiplexer_108 (
    .in0(multiplexer_117_out), .in1({2'b00, middle_rocket_pixel_right, 2'b00}), .out(multiplexer_108_out),
    .sel(b_pressed));  // open: en
  or or_7 (or_7_out, pull_resistor_3_node, transistor_5_out);
  not not_13 (not_13_out, bot_enabled);
  Transistor #(.\type ("n")) transistor_4 (.in(power), .out(pull_resistor_3_node), .gate(b_pressed));
  Transistor #(.\type ("n"), .gate("br")) transistor_5 (
    .in(frequency_divider_1_out), .out(transistor_5_out), .gate(and_1_out));
  Multiplexer #(.select(3), .width(8)) multiplexer_109 (
    .in0(8'hc), .in1(8'h8), .in2(8'h6), .in3(8'h4), .in4(8'h3), .in5(8'h2), .out(multiplexer_109_out),
    .sel(aoa));  // open: in6, in7, en
  assign bit_extender_2_out = {{2{1'b0}}, dmx_x_cord};  // Bit_Extender bit_extender_2
  // Probe on keyboard_t
  // Probe on keyboard_t
  Comparator #(.mode("unsigned")) comparator_1 (.a(p1_score_bin), .b(8'h2), .eq(win));  // open: gt, lt
  Comparator #(.mode("unsigned")) comparator_2 (.a(8'h2), .b(p2_score_bin), .eq(comparator_2_eq));  // open: gt, lt
  comp_y_cord comp_y_cord_1 (.in_1(player1), .in_2(cord11), .\шарик (isDown), .out_4(swap_x_dir_left_r_to_left));
  comp_y_cord comp_y_cord_2 (.in_1(racket2), .in_2(cord22), .\шарик (isDown), .out_4(swap_x_dir_right_r_to_right));
  and and_1 (and_1_out, bot_enabled, enable_move);
  frequency_divider frequency_divider_1 (
    .IN(power), .OUT(frequency_divider_1_out), .n(multiplexer_109_out));  // open: _0
  Multiplexer #(.width(8)) multiplexer_110 (
    .in0({8{1'b0}}), .in1(bit_extender_2_out), .out(multiplexer_110_out), .sel(enable_move));  // open: en
  assign bit_extender_3_out = {{3{1'b0}}, prev_val};  // Bit_Extender bit_extender_3
  Comparator #(.width(7)) comparator_3 (.a(7'b1110011), .b(keyboard_t), .eq(s_button));  // open: gt, lt
  Comparator #(.width(7)) comparator_4 (.a(keyboard_t), .b(7'b1110111), .eq(w_button));  // open: gt, lt
  Comparator #(.width(7)) comparator_5 (.a(7'b1101100), .b(keyboard_t), .eq(L_button));  // open: gt, lt
  Comparator #(.width(7)) comparator_6 (.a(keyboard_t), .b(7'b1101111), .eq(o_button));  // open: gt, lt
  or or_8 (gameover, win, comparator_2_eq);
  bot_borris bot_borris_1 (
    .New_Y(bot_borris_1_new_y), .X(multiplexer_110_out), .Y(bit_extender_3_out), .Vx(x_speed), .Vy(y_speed));
  comp_y_cord comp_y_cord_3 (.in_1(racket2), .in_2(cord2), .\шарик (isDown), .out_4(r2));
  or or_9 (swap_x_direction_right_wall, r2, fail2);
  comp_y_cord comp_y_cord_4 (.in_1(player1), .in_2(cord1), .\шарик (isDown), .out_4(r1));
  or or_10 (swap_x_direction_left_wall, r1, fail1);
  Multiplexer #(.width(32)) multiplexer_111 (.in0(player2), .in1(bot), .out(racket2), .sel(bot_enabled));  // open: en
  Adder #(.width(32)) adder_1 (.a(register_1_q), .b(32'h1), .out(adder_1_out));  // open: cin, cout
  Comparator #(.width(32)) comparator_7 (.a(register_1_q), .b({32{1'b0}}), .eq(comparator_7_eq));  // open: gt, lt
  Pull_Resistor pull_resistor_4 (.node(transistor_5_out));
  or or_11 (or_11_out, s_button, restart);
  not not_14 (not_14_out, restart);
  or or_12 (or_12_out, s_button, restart, w_button);
  or or_13 (or_13_out, L_button, restart);
  not not_15 (not_15_out, restart);
  or or_14 (or_14_out, L_button, restart, o_button);
  Multiplexer #(.width(32)) multiplexer_112 (
    .in0(register_1_q), .in1(adder_1_out), .out(multiplexer_112_out), .sel(comparator_7_eq));  // open: en
  Register #(.width(5)) register_2 (
    .D({undriven[4], bot_borris_1_new_y[3:0]}), .Q(register_2_q), .clk(transistor_6_out));  // open: en, clr
  Transistor #(.\type ("n"), .gate("br")) transistor_6 (.in(power), .out(transistor_6_out), .gate(enable_move));
  Counter #(.width(5), .max('h1b), .ongoal("stay")) counter_1 (
    .load(or_11_out), .D(5'b01101), .count(not_14_out), .Q(counter_1_q), .clk(or_12_out));  // open: carry, clr
  Counter #(.width(5), .max('h1b), .ongoal("stay")) counter_2 (
    .load(or_13_out), .D(5'b01101), .count(not_15_out), .Q(counter_2_q), .clk(or_14_out));  // open: carry, clr
  Shifter #(.width(32)) shifter_1 (.in(multiplexer_112_out), .\dist (5'b00001), .out(shifter_1_out));
  Shifter #(.width(32), .shift("lr")) shifter_2 (.in(multiplexer_112_out), .\dist (5'b00001), .out(shifter_2_out));
  Comparator #(.width(32)) comparator_8 (
    .a(multiplexer_112_out), .b(whereMoveBot), .gt(bot_down), .eq(comparator_8_eq));  // open: lt
  Decoder #(.select(5)) decoder_1 (
    .out0(whereMoveBot[0]), .out1(whereMoveBot[1]), .out2(whereMoveBot[2]), .out3(whereMoveBot[3]),
    .out4(whereMoveBot[4]), .out5(whereMoveBot[5]), .out6(whereMoveBot[6]), .out7(whereMoveBot[7]),
    .out8(whereMoveBot[8]), .out9(whereMoveBot[9]), .out10(whereMoveBot[10]), .out11(whereMoveBot[11]),
    .out12(whereMoveBot[12]), .out13(whereMoveBot[13]), .out14(whereMoveBot[14]), .out15(whereMoveBot[15]),
    .out16(whereMoveBot[16]), .out17(whereMoveBot[17]), .out18(whereMoveBot[18]), .out19(whereMoveBot[19]),
    .out20(whereMoveBot[20]), .out21(whereMoveBot[21]), .out22(whereMoveBot[22]), .out23(whereMoveBot[23]),
    .out24(whereMoveBot[24]), .out25(whereMoveBot[25]), .out26(whereMoveBot[26]), .out27(whereMoveBot[27]),
    .out28(whereMoveBot[28]), .out29(whereMoveBot[29]), .out30(whereMoveBot[30]), .out31(whereMoveBot[31]),
    .sel(register_2_q));  // open: en
  Decoder #(.select(5), .disabled(0)) decoder_2 (
    .out0(decoder_2_out0[2]), .out1(decoder_2_out0[3]), .out2(decoder_2_out0[4]), .out3(decoder_2_out0[5]),
    .out4(decoder_2_out0[6]), .out5(decoder_2_out0[7]), .out6(decoder_2_out0[8]), .out7(decoder_2_out0[9]),
    .out8(decoder_2_out0[10]), .out9(decoder_2_out0[11]), .out10(decoder_2_out0[12]),
    .out11(decoder_2_out0[13]), .out12(decoder_2_out0[14]), .out13(decoder_2_out0[15]),
    .out14(decoder_2_out0[16]), .out15(decoder_2_out0[17]), .out16(decoder_2_out0[18]),
    .out17(decoder_2_out0[19]), .out18(decoder_2_out0[20]), .out19(decoder_2_out0[21]),
    .out20(decoder_2_out0[22]), .out21(decoder_2_out0[23]), .out22(decoder_2_out0[24]),
    .out23(decoder_2_out0[25]), .out24(decoder_2_out0[26]), .out25(decoder_2_out0[27]),
    .out26(decoder_2_out0[28]), .out27(decoder_2_out0[29]), .sel(counter_1_q));  // open: out28, out29, out30, out31, en
  Decoder #(.select(5), .disabled(0)) decoder_3 (
    .out0(middle_rocket_pixel_right[2]), .out1(middle_rocket_pixel_right[3]),
    .out2(middle_rocket_pixel_right[4]), .out3(middle_rocket_pixel_right[5]),
    .out4(middle_rocket_pixel_right[6]), .out5(middle_rocket_pixel_right[7]),
    .out6(middle_rocket_pixel_right[8]), .out7(middle_rocket_pixel_right[9]),
    .out8(middle_rocket_pixel_right[10]), .out9(middle_rocket_pixel_right[11]),
    .out10(middle_rocket_pixel_right[12]), .out11(middle_rocket_pixel_right[13]),
    .out12(middle_rocket_pixel_right[14]), .out13(middle_rocket_pixel_right[15]),
    .out14(middle_rocket_pixel_right[16]), .out15(middle_rocket_pixel_right[17]),
    .out16(middle_rocket_pixel_right[18]), .out17(middle_rocket_pixel_right[19]),
    .out18(middle_rocket_pixel_right[20]), .out19(middle_rocket_pixel_right[21]),
    .out20(middle_rocket_pixel_right[22]), .out21(middle_rocket_pixel_right[23]),
    .out22(middle_rocket_pixel_right[24]), .out23(middle_rocket_pixel_right[25]),
    .out24(middle_rocket_pixel_right[26]), .out25(middle_rocket_pixel_right[27]),
    .out26(middle_rocket_pixel_right[28]), .out27(middle_rocket_pixel_right[29]), .sel(counter_2_q));  // open: out28, out29, out30, out31, en
  Comparator #(.width(32)) comparator_9 (.a(shifter_1_out), .b(32'h20000000), .gt(comparator_9_gt));  // open: eq, lt
  Comparator #(.width(32)) comparator_10 (.a(shifter_2_out), .b(32'h4), .lt(comparator_10_lt));  // open: gt, eq
  Adder #(.width(5)) adder_2 (.a(counter_1_q), .b(5'b00001), .out(middle_rocket_pixel_left));  // open: cin, cout
  Multiplexer #(.width(32)) multiplexer_113 (
    .in0(shifter_1_out), .in1(multiplexer_112_out), .out(multiplexer_113_out), .sel(comparator_9_gt));  // open: en
  Multiplexer #(.width(32)) multiplexer_114 (
    .in0(shifter_2_out), .in1(multiplexer_112_out), .out(multiplexer_114_out), .sel(comparator_10_lt));  // open: en
  not not_16 (not_16_out, isLeft);
  // Probe on dmx_x_cord
  Counter #(.ongoal("continue")) counter_3 (
    .Q(p2_score_bin), .clk(fail1), .clr(restart));  // open: load, D, count, carry
  Counter #(.ongoal("continue")) counter_4 (
    .Q(p1_score_bin), .clk(fail2), .clr(restart));  // open: load, D, count, carry
  Clock clock_1 (.out(keyboard_power));
  pause pause_1 (._14_y(D29), ._15_y(D30), ._13_y(D31), ._16_y(D32), ._18_y(D33), ._17_y(D34), .is_0_up(is_ball_16));
  Multiplexer #(.width(32)) multiplexer_115 (
    .in0(32'h1e), .in1(32'h78000000), .out(y_pause_cord), .sel(is_ball_16));  // open: en
  Multiplexer #(.width(32)) multiplexer_116 (
    .in0(multiplexer_113_out), .in1(multiplexer_114_out), .out(multiplexer_116_out), .sel(bot_down));  // open: en
  Multiplexer #(.width(32)) multiplexer_117 (
    .in0(multiplexer_116_out), .in1(multiplexer_112_out), .out(multiplexer_117_out), .sel(comparator_8_eq));  // open: en
  Comparator #(.width(6)) comparator_11 (.a(dmx_x_cord), .b(6'b010001), .eq(comparator_11_eq));  // open: gt, lt
  and and_2 (and_2_out, comparator_11_eq, not_16_out);
  Multiplexer #(.width(8)) multiplexer_118 (
    .in0(8'h2), .in1({8{1'b0}}), .out(multiplexer_118_out), .sel(pause));  // open: en
  Transistor #(.\type ("n")) transistor_7 (.in(keyboard_power), .out(transistor_7_out), .gate(playing));
  Pull_Resistor pull_resistor_5 (.node(is_ball_16));
  // Probe on y_pause_cord
  Multiplexer #(.width(32)) multiplexer_119 (
    .in0(register_1_q), .in1(multiplexer_117_out), .out(multiplexer_119_out), .sel(enable_move));  // open: en
  D_Flip_Flop d_ff_1 (.Q(enable_move), .preset(and_2_out), .reset(isLeft));  // open: clk, D, Qn, en
  nor nor_1 (fail1, dmx_x_cord[0], dmx_x_cord[1], dmx_x_cord[2], dmx_x_cord[3], dmx_x_cord[4], dmx_x_cord[5]);
  and and_3 (fail2, dmx_x_cord[0], dmx_x_cord[1], dmx_x_cord[2], dmx_x_cord[4], dmx_x_cord[5], dmx_x_cord[3]);
  bcd bcd_1 (._8bit_Input(p2_score_bin), .BCD_Output({out_37, out_38, out_39}));
  bcd bcd_2 (._8bit_Input(p1_score_bin), .BCD_Output({out_2, out_3, out_4}));
  frequency_divider frequency_divider_2 (.IN(transistor_7_out), .OUT(power), .n(multiplexer_118_out));  // open: _0
  Shifter #(.width(32)) shifter_3 (.in(multiplexer_119_out), .\dist (5'b00001), .out(shifter_3_out));
  Shifter #(.width(32)) shifter_4 (.in(multiplexer_119_out), .\dist (5'b00010), .out(shifter_4_out));
  Shifter #(.width(32), .shift("lr")) shifter_5 (.in(multiplexer_119_out), .\dist (5'b00010), .out(shifter_5_out));
  Shifter #(.width(32), .shift("lr")) shifter_6 (.in(multiplexer_119_out), .\dist (5'b00001), .out(shifter_6_out));
  assign bot = shifter_3_out | shifter_4_out | multiplexer_119_out | shifter_5_out | shifter_6_out;  // OR_Gate or_15, 32 bits wide
  Shifter #(.width(32)) shifter_7 (.in({2'b00, decoder_2_out0, 2'b00}), .\dist (5'b00001), .out(shifter_7_out));
  Shifter #(.width(32)) shifter_8 (.in({2'b00, decoder_2_out0, 2'b00}), .\dist (5'b00010), .out(shifter_8_out));
  Shifter #(.width(32), .shift("lr")) shifter_9 (
    .in({2'b00, decoder_2_out0, 2'b00}), .\dist (5'b00010), .out(shifter_9_out));
  Shifter #(.width(32), .shift("lr")) shifter_10 (
    .in({2'b00, decoder_2_out0, 2'b00}), .\dist (5'b00001), .out(shifter_10_out));
  Shifter #(.width(32)) shifter_11 (
    .in({2'b00, middle_rocket_pixel_right, 2'b00}), .\dist (5'b00001), .out(shifter_11_out));
  Shifter #(.width(32)) shifter_12 (
    .in({2'b00, middle_rocket_pixel_right, 2'b00}), .\dist (5'b00010), .out(shifter_12_out));
  Shifter #(.width(32), .shift("lr")) shifter_13 (
    .in({2'b00, middle_rocket_pixel_right, 2'b00}), .\dist (5'b00010), .out(shifter_13_out));
  Shifter #(.width(32), .shift("lr")) shifter_14 (
    .in({2'b00, middle_rocket_pixel_right, 2'b00}), .\dist (5'b00001), .out(shifter_14_out));
  not not_17 (not_17_out, bot_down);
  and and_4 (and_4_out, not_17_out, bot_enabled);
  and and_5 (and_5_out, bot_down, bot_enabled);
  not not_18 (not_18_out, bot_down);
  and and_6 (and_6_out, not_18_out, bot_enabled);
  and and_7 (and_7_out, bot_down, bot_enabled);
  Comparator #(.width(5)) comparator_12 (.a(dmx_x_cord_L), .b(5'b00100), .eq(comparator_12_eq));  // open: gt, lt
  Comparator #(.width(5)) comparator_13 (.a(dmx_x_cord_L), .b(5'b00100), .eq(comparator_13_eq));  // open: gt, lt
  or or_16 (or_16_out, o_pressed, and_4_out);
  Comparator #(.width(5)) comparator_14 (.a(dmx_x_cord_R), .b(5'b11011), .eq(comparator_14_eq));  // open: gt, lt
  or or_17 (or_17_out, l_pressed, and_5_out);
  Comparator #(.width(5)) comparator_15 (.a(dmx_x_cord_R), .b(5'b11011), .eq(comparator_15_eq));  // open: gt, lt
  Comparator #(.width(5)) comparator_16 (.a(dmx_x_cord_L), .b(5'b00100), .eq(comparator_16_eq));  // open: gt, lt
  Comparator #(.width(5)) comparator_17 (.a(dmx_x_cord_L), .b(5'b00100), .eq(comparator_17_eq));  // open: gt, lt
  or or_18 (or_18_out, o_pressed, and_6_out);
  Comparator #(.width(5)) comparator_18 (.a(dmx_x_cord_R), .b(5'b11011), .eq(comparator_18_eq));  // open: gt, lt
  or or_19 (or_19_out, l_pressed, and_7_out);
  Comparator #(.width(5)) comparator_19 (.a(dmx_x_cord_R), .b(5'b11011), .eq(comparator_19_eq));  // open: gt, lt
  // Probe on player1
  assign player1 = shifter_7_out | shifter_8_out | {2'b00, decoder_2_out0, 2'b00} | shifter_9_out | shifter_10_out;  // OR_Gate or_20, 32 bits wide
  // Probe on player2
  assign player2 = shifter_11_out | shifter_12_out | {2'b00, middle_rocket_pixel_right, 2'b00} | shifter_13_out | shifter_14_out;  // OR_Gate or_21, 32 bits wide
  not not_19 (not_19_out, isLeft);
  not not_20 (not_20_out, isLeft);
  not not_21 (not_21_out, isLeft);
  not not_22 (not_22_out, isLeft);
  not not_23 (not_23_out, isDown);
  not not_24 (not_24_out, isDown);
  not not_25 (not_25_out, isDown);
  not not_26 (not_26_out, isDown);
  or or_22 (or_22_out, space_pressed, rest_pressed);
  or or_23 (or_23_out, space_pressed, rest_pressed);
  // Probe on keyboard_t
  // Probe on keyboard_t
  // Probe on keyboard_t
  // Probe on keyboard_t
  and and_8 (and_8_out, r1, isDown, w_pressed, comparator_12_eq, isLeft);
  and and_9 (and_9_out, r1, not_23_out, s_pressed, comparator_13_eq, isLeft);
  and and_10 (and_10_out, r2, isDown, or_16_out, comparator_14_eq, not_19_out);
  and and_11 (and_11_out, r2, not_24_out, or_17_out, comparator_15_eq, not_20_out);
  and and_12 (and_12_out, r1, not_25_out, w_pressed, comparator_16_eq, isLeft);
  and and_13 (and_13_out, r1, isDown, s_pressed, comparator_17_eq, isLeft);
  and and_14 (and_14_out, r2, not_26_out, or_18_out, comparator_18_eq, not_21_out);
  and and_15 (and_15_out, r2, isDown, or_19_out, comparator_19_eq, not_22_out);
  Multiplexer #(.width(5)) multiplexer_120 (
    .in0(prev_val), .in1(middle_rocket_pixel_left), .out(multiplexer_120_out), .sel(or_22_out));  // open: en
  // Probe on y_speed
  Multiplexer #(.select(3), .width(8)) multiplexer_121 (
    .in0(8'hc), .in1(8'h8), .in2(8'h6), .in3(8'h4), .in4(8'h3), .in5(8'h2), .out(y_speed), .sel(aoa));  // open: in6, in7, en
  Multiplexer #(.width(6)) multiplexer_122 (
    .in0(dmx_x_cord), .in1(6'b000100), .out(multiplexer_122_out), .sel(or_23_out));  // open: en
  Multiplexer #(.select(3), .width(8)) multiplexer_123 (
    .in0(8'h2), .in1(8'h3), .in2(8'h4), .in3(8'h6), .in4(8'h8), .in5(8'hc), .out(x_speed), .sel(aoa));  // open: in6, in7, en
  Comparator #(.width(7)) comparator_20 (.a(keyboard_t), .b(7'b0100000), .eq(space_pr));  // open: gt, lt
  Comparator #(.width(7)) comparator_21 (.a(keyboard_t), .b(7'b1110000), .eq(comparator_21_eq));  // open: gt, lt
  Comparator #(.width(7)) comparator_22 (.a(keyboard_t), .b(7'b1100010), .eq(b_button));  // open: gt, lt
  Comparator #(.width(7)) comparator_23 (.a(keyboard_t), .b(7'b1110010), .eq(restart));  // open: gt, lt
  or or_24 (or_24_out, and_8_out, and_9_out, and_10_out, and_11_out);
  or or_25 (P, and_12_out, and_13_out, and_14_out, and_15_out);
  or or_26 (or_26_out, isDown, or_22_out);
  frequency_divider frequency_divider_3 (.IN(power), .OUT(frequency_divider_3_out), .n(y_speed));  // open: _0
  or or_27 (or_27_out, isLeft, or_23_out);
  frequency_divider frequency_divider_4 (.IN(power), .OUT(frequency_divider_4_out), .n(x_speed));  // open: _0
  or or_28 (or_28_out, or_24_out, P);
  Counter #(.width(5), .max('h1f)) counter_5 (
    .load(or_26_out), .D(multiplexer_120_out), .count(not_27_out), .Q(prev_val),
    .clk(frequency_divider_3_out), .clr(restart));  // open: carry
  not not_27 (not_27_out, or_22_out);
  assign dmx_x_cord = counter_6_q;  // Buffer buffer_1, 6 bits wide
  Counter #(.width(6), .max('h3f)) counter_6 (
    .load(or_27_out), .D(multiplexer_122_out), .count(not_28_out), .Q(counter_6_q),
    .clk(frequency_divider_4_out), .clr(restart));  // open: carry
  not not_28 (not_28_out, or_23_out);
  D_Flip_Flop d_ff_2 (.clk(space_pr), .D(space_pr), .Q(d_ff_2_q), .reset(restart));  // open: Qn, preset, en
  T_Flip_Flop t_ff_1 (.clk(comparator_21_eq), .T(comparator_21_eq), .Q(t_ff_1_q));  // open: Qn, preset, reset, en
  T_Flip_Flop t_ff_2 (.clk(b_button), .T(b_button), .Q(bot_enabled));  // open: Qn, preset, reset, en
  Decoder #(.select(5)) decoder_4 (
    .out0(dmx_y_cord[0]), .out1(dmx_y_cord[1]), .out2(dmx_y_cord[2]), .out3(dmx_y_cord[3]),
    .out4(dmx_y_cord[4]), .out5(dmx_y_cord[5]), .out6(dmx_y_cord[6]), .out7(dmx_y_cord[7]),
    .out8(dmx_y_cord[8]), .out9(dmx_y_cord[9]), .out10(dmx_y_cord[10]), .out11(dmx_y_cord[11]),
    .out12(dmx_y_cord[12]), .out13(dmx_y_cord[13]), .out14(dmx_y_cord[14]), .out15(dmx_y_cord[15]),
    .out16(dmx_y_cord[16]), .out17(dmx_y_cord[17]), .out18(dmx_y_cord[18]), .out19(dmx_y_cord[19]),
    .out20(dmx_y_cord[20]), .out21(dmx_y_cord[21]), .out22(dmx_y_cord[22]), .out23(dmx_y_cord[23]),
    .out24(dmx_y_cord[24]), .out25(dmx_y_cord[25]), .out26(dmx_y_cord[26]), .out27(dmx_y_cord[27]),
    .out28(dmx_y_cord[28]), .out29(dmx_y_cord[29]), .out30(dmx_y_cord[30]), .out31(dmx_y_cord[31]),
    .sel(prev_val));  // open: en
  // Probe on counter_6_q
  and and_16 (playing, d_ff_2_q, ~gameover);  // AND_Gate
  or or_29 (pause, t_ff_1_q, gameover);
  not not_29 (not_29_out, P);
  Counter #(.width(3), .max('h5), .ongoal("stay")) counter_7 (
    .load(not_29_out), .D(3'b000), .count(not_30_out), .Q(aoa), .clk(or_30_out));  // open: carry, clr
  not not_30 (not_30_out, restart);
  or or_30 (or_30_out, restart, or_28_out);
  // Probe on aoa
  Demultiplexer #(.width(5)) demultiplexer_3 (
    .out0(dmx_x_cord_L), .out1(dmx_x_cord_R), .in(counter_6_q[4:0]), .sel(counter_6_q[5]));  // open: en
  or or_31 (or_31_out, swap_x_direction_right_wall, swap_x_dir_left_r_to_left);
  or or_32 (or_32_out, swap_x_direction_left_wall, swap_x_dir_right_r_to_right);
  // Probe on dmx_y_cord
  D_Flip_Flop d_ff_3 (.Q(isLeft), .preset(or_31_out), .reset(or_32_out));  // open: clk, D, Qn, en
  last_button_press last_button_press_1 (
    .button(w_button), .opposite_button(s_button), .button_pressed(w_pressed), .power(keyboard_power));
  last_button_press last_button_press_2 (
    .button(s_button), .opposite_button(w_button), .button_pressed(s_pressed), .power(keyboard_power));
  last_button_press last_button_press_3 (
    .button(o_button), .opposite_button(l_button_t), .button_pressed(o_pressed), .power(keyboard_power));
  last_button_press last_button_press_4 (
    .button(l_button_t), .opposite_button(o_button), .button_pressed(l_pressed), .power(keyboard_power));
  D_Flip_Flop d_ff_4 (.Q(isDown), .preset(dmx_y_cord[31]), .reset(dmx_y_cord[0]));  // open: clk, D, Qn, en
  last_button_press last_button_press_5 (
    .button(space_pr), .opposite_button(l_button_t), .button_pressed(space_pressed), .power(keyboard_power));
  last_button_press last_button_press_6 (
    .button(restart), .opposite_button(l_button_t), .button_pressed(rest_pressed), .power(keyboard_power));
  last_button_press last_button_press_7 (
    .button(b_button), .button_pressed(b_pressed), .power(keyboard_power));  // open: opposite_button

  // Other names for the same wires on the sheet: D4[31:0] = cord1; D59[31:0] = cord2; D2[31:0] = cord11;
  //   D61[31:0] = cord22; kpower = keyboard_power; n0[31:0] = out_5; n1[31:0] = out_6; n2[31:0] = out_7;
  //   n3[31:0] = out_8; n4[31:0] = out_9; n5[31:0] = out_10; n6[31:0] = out_11; n7[31:0] = out_12; n8[31:0] = out_13;
  //   n9[31:0] = out_14; n10[31:0] = out_15; n11[31:0] = out_16; n12[31:0] = out_17; n13[31:0] = out_18;
  //   n14[31:0] = out_19; n15[31:0] = out_20; n16[31:0] = out_21; n17[31:0] = out_22; n18[31:0] = out_23;
  //   n19[31:0] = out_24; n20[31:0] = out_25; n21[31:0] = out_26; n22[31:0] = out_27; n23[31:0] = out_28;
  //   n24[31:0] = out_29; n25[31:0] = out_30; n26[31:0] = out_31; n27[31:0] = out_32; n28[31:0] = out_33;
  //   n29[31:0] = out_34; n30[31:0] = out_35; n31[31:0] = out_36; p1_score[11:0] = {out_2, out_3, out_4};
  //   p2_score[11:0] = {out_37, out_38, out_39}; racket1[31:0] = player1;
  //   racket2_3pix[29:2] = middle_rocket_pixel_right; S6[15:0] = S5; S11[15:0] = S10; S16[15:0] = S15;
  //   S21[15:0] = S20; S26[15:0] = S25; tunnel[1:0] = {pause, playing}; vec_adr[31:0] = bot

  // Notes on the sheet:
  //   video out
  //   win / lose screen
  //   SCORE
  //   Player 1
  //   Playing scene
  //   PRESS SPACE
  //   Inputs
  //   Pause - P
  //   Restart - R
  //   Bot - B
  //   Player 1 - W and S
  //   Player 2 - O and L
  //   Start game - SPACE
  //   Scene select
  //   00 - start scene
  //   01 - playing scene
  //   10 - gameover scene
  //   11 - pause scene
  //   SCORE
  //   Player 2
  //   PLAYER_1
  //   PLAYER_2
  //   Keyboard input
  //   Keyboard input
  //   отскок между ракеткой и стенкой
  //   BOT (Skynet in future)
  //   если попадание: правая стенка
  //   если попадание: левая стенка
  //   неработающие варианты проверки на столкновение
  //   Gameover check
  //   Goal check
  //   Power
  //   pause screen
  //   Score count and print
  //   проверка на положение мяча
  //   запись координат паузы
  //   движение правой ракетки когда бот активен
  //   уменьшение угла
  //   увеличение угла
  //   Keyboard input
  //   угол наклона мячика
  //   Запоминание последней кнопки
  //   движение по оси Y
  //   движение по оси X
  //   WARNING: я хз почему, но если передвигать этот чип - то логисим зависает
endmodule

// ||
module comp_y_cord (
  input  [31:0] in_1,
  input  [31:0] in_2,
  input  \шарик ,
  output out_4
);

  wire or_1_out, or_2_out, or_3_out, or_4_out, or_5_out;
  wire [29:0] and_2_out, and_3_out;
  wire [31:0] and_1_out;

  assign and_1_out = in_1 & in_2;  // AND_Gate and_1, 32 bits wide
  assign and_2_out = in_1[30:1] & in_2[29:0];  // AND_Gate and_2, 30 bits wide
  or or_1 (or_1_out, and_1_out[0], and_1_out[1], and_1_out[2], and_1_out[3], and_1_out[4], and_1_out[5], and_1_out[6], and_1_out[7], and_1_out[8], and_1_out[9], and_1_out[10], and_1_out[11], and_1_out[12], and_1_out[13], and_1_out[14], and_1_out[15], and_1_out[17], and_1_out[18], and_1_out[19], and_1_out[20], and_1_out[21], and_1_out[22], and_1_out[23], and_1_out[24], and_1_out[25], and_1_out[26], and_1_out[27], and_1_out[28], and_1_out[29], and_1_out[30], and_1_out[31], and_1_out[16]);
  assign and_3_out = in_1[30:1] & in_2[31:2];  // AND_Gate and_3, 30 bits wide
  or or_2 (or_2_out, and_2_out[0], and_2_out[1], and_2_out[2], and_2_out[3], and_2_out[4], and_2_out[5], and_2_out[6], and_2_out[7], and_2_out[8], and_2_out[9], and_2_out[10], and_2_out[11], and_2_out[12], and_2_out[13], and_2_out[14], and_2_out[16], and_2_out[17], and_2_out[18], and_2_out[19], and_2_out[20], and_2_out[21], and_2_out[22], and_2_out[23], and_2_out[24], and_2_out[25], and_2_out[26], and_2_out[27], and_2_out[28], and_2_out[29], and_2_out[15]);
  or or_3 (or_3_out, and_3_out[0], and_3_out[1], and_3_out[2], and_3_out[3], and_3_out[4], and_3_out[5], and_3_out[6], and_3_out[7], and_3_out[8], and_3_out[9], and_3_out[10], and_3_out[11], and_3_out[12], and_3_out[13], and_3_out[14], and_3_out[16], and_3_out[17], and_3_out[18], and_3_out[19], and_3_out[20], and_3_out[21], and_3_out[22], and_3_out[23], and_3_out[24], and_3_out[25], and_3_out[26], and_3_out[27], and_3_out[28], and_3_out[29], and_3_out[15]);
  or or_4 (or_4_out, or_1_out, or_3_out);
  or or_5 (or_5_out, or_1_out, or_2_out);
  Multiplexer multiplexer_1 (.in0(or_5_out), .in1(or_4_out), .out(out_4), .sel(\шарик ));  // open: en

  // Other names for the same wires on the sheet: ball_cord_y[31:0] = in_2; rock_cord_y[31:0] = in_1;
  //   _1_down = \шарик 

  // Notes on the sheet:
  //   ракетка
  //   снизу вверх
  //   сверху вниз
endmodule

module parseScore (
  input  [7:0] in_1,
  output [3:0] out_2,
  output [3:0] out_3,
  output [3:0] out_4
);

  wire [7:0] divider_1_out, divider_2_out, multiplier_1_out, multiplier_2_out, subtractor_1_out,
       subtractor_2_out;

  // Probe on in_1
  // Probe on divider_1_out
  Divider divider_1 (.a(in_1), .b(8'ha), .out(divider_1_out));  // open: upper, rem
  Divider divider_2 (.a(divider_1_out), .b(8'ha), .out(divider_2_out));  // open: upper, rem
  Multiplier multiplier_1 (.a(divider_1_out), .b(8'ha), .out(multiplier_1_out));  // open: cin, cout
  // Probe on multiplier_1_out
  // Probe on multiplier_2_out
  Multiplier multiplier_2 (.a(divider_2_out), .b(8'ha), .out(multiplier_2_out));  // open: cin, cout
  Bit_Extender #(.out_width(4)) bit_extender_1 (.in(divider_2_out), .out(out_2));
  Subtractor subtractor_1 (.a(in_1), .b(multiplier_1_out), .out(subtractor_1_out));  // open: bin, bout
  // Probe on out_2
  // Probe on subtractor_2_out
  Subtractor subtractor_2 (.a(divider_1_out), .b(multiplier_2_out), .out(subtractor_2_out));  // open: bin, bout
  // Probe on subtractor_1_out
  Bit_Extender #(.out_width(4)) bit_extender_2 (.in(subtractor_2_out), .out(out_3));
  Bit_Extender #(.out_width(4)) bit_extender_3 (.in(subtractor_1_out), .out(out_4));

  // Notes on the sheet:
  //   OBSOLETE
  //   as of v0.1.3
endmodule

module frequency_divider (
  input  [7:0] n,
  input  IN,
  input  _0,
  output OUT
);

  wire comparator_1_eq, comparator_1_lt, or_1_out, or_2_out;
  wire [7:0] counter_1_q;

  Counter counter_1 (.count(IN), .Q(counter_1_q), .clk(IN), .clr(or_1_out));  // open: load, D, carry
  or or_1 (or_1_out, _0, or_2_out);
  Comparator #(.mode("unsigned")) comparator_1 (
    .a(n), .b(counter_1_q), .eq(comparator_1_eq), .lt(comparator_1_lt));  // open: gt
  or or_2 (or_2_out, comparator_1_eq, comparator_1_lt);
  T_Flip_Flop t_ff_1 (.clk(or_2_out), .T(or_2_out), .Q(OUT), .reset(_0));  // open: Qn, preset, en
endmodule

module bcd (
  input  [7:0] _8bit_Input,
  output [11:0] BCD_Output
);

  wire [3:0] bcd_helper_1_out, bcd_helper_2_out, bcd_helper_3_out, bcd_helper_4_out, bcd_helper_5_out,
       bcd_helper_6_out, bcd_helper_7_out, bcd_helper_8_out, bcd_helper_9_out, bcd_helper_10_out,
       bcd_helper_11_out, bcd_helper_12_out, bcd_helper_13_out, bcd_helper_14_out, bcd_helper_15_out,
       bcd_helper_16_out, bcd_helper_17_out, bcd_helper_18_out;
  wire [3:3] bcd_helper_21_out;

  // Probe on _8bit_Input
  bcd_helper bcd_helper_1 (.inp({3'b000, _8bit_Input[7]}), .out(bcd_helper_1_out));
  bcd_helper bcd_helper_2 (.inp(4'b0000), .out(bcd_helper_2_out));
  bcd_helper bcd_helper_3 (.inp(4'b0000), .out(bcd_helper_3_out));
  bcd_helper bcd_helper_4 (.inp({bcd_helper_1_out[2:0], _8bit_Input[6]}), .out(bcd_helper_4_out));
  bcd_helper bcd_helper_5 (.inp({bcd_helper_2_out[2:0], bcd_helper_1_out[3]}), .out(bcd_helper_5_out));
  bcd_helper bcd_helper_6 (.inp({bcd_helper_3_out[2:0], bcd_helper_2_out[3]}), .out(bcd_helper_6_out));
  bcd_helper bcd_helper_7 (.inp({bcd_helper_4_out[2:0], _8bit_Input[5]}), .out(bcd_helper_7_out));
  bcd_helper bcd_helper_8 (.inp({bcd_helper_5_out[2:0], bcd_helper_4_out[3]}), .out(bcd_helper_8_out));
  bcd_helper bcd_helper_9 (.inp({bcd_helper_6_out[2:0], bcd_helper_5_out[3]}), .out(bcd_helper_9_out));
  bcd_helper bcd_helper_10 (.inp({bcd_helper_7_out[2:0], _8bit_Input[4]}), .out(bcd_helper_10_out));
  bcd_helper bcd_helper_11 (.inp({bcd_helper_8_out[2:0], bcd_helper_7_out[3]}), .out(bcd_helper_11_out));
  bcd_helper bcd_helper_12 (.inp({bcd_helper_9_out[2:0], bcd_helper_8_out[3]}), .out(bcd_helper_12_out));
  bcd_helper bcd_helper_13 (.inp({bcd_helper_10_out[2:0], _8bit_Input[3]}), .out(bcd_helper_13_out));
  bcd_helper bcd_helper_14 (.inp({bcd_helper_11_out[2:0], bcd_helper_10_out[3]}), .out(bcd_helper_14_out));
  bcd_helper bcd_helper_15 (.inp({bcd_helper_12_out[2:0], bcd_helper_11_out[3]}), .out(bcd_helper_15_out));
  bcd_helper bcd_helper_16 (.inp({bcd_helper_13_out[2:0], _8bit_Input[2]}), .out(bcd_helper_16_out));
  bcd_helper bcd_helper_17 (.inp({bcd_helper_14_out[2:0], bcd_helper_13_out[3]}), .out(bcd_helper_17_out));
  bcd_helper bcd_helper_18 (.inp({bcd_helper_15_out[2:0], bcd_helper_14_out[3]}), .out(bcd_helper_18_out));
  bcd_helper bcd_helper_19 (.inp({bcd_helper_16_out[2:0], _8bit_Input[1]}), .out(BCD_Output[4:1]));
  bcd_helper bcd_helper_20 (.inp({bcd_helper_17_out[2:0], bcd_helper_16_out[3]}), .out(BCD_Output[8:5]));
  bcd_helper bcd_helper_21 (
    .inp({bcd_helper_18_out[2:0], bcd_helper_17_out[3]}), .out({bcd_helper_21_out[3], BCD_Output[11:9]}));
  // Probe on BCD_Output[11:8]
  // Probe on BCD_Output[7:4]
  // Probe on {BCD_Output[3:1], _8bit_Input[0]}

  assign BCD_Output[0] = _8bit_Input[0];

  // Notes on the sheet:
  //   The double dable algorithm
endmodule

module bcd_helper (
  input  [3:0] inp,
  output [3:0] out
);

  wire comparator_1_eq, comparator_1_lt, or_1_out;
  wire [3:0] adder_1_out;

  // Probe on inp
  Adder #(.width(4)) adder_1 (.a(4'b0011), .b(inp), .out(adder_1_out));  // open: cin, cout
  Comparator #(.width(4), .mode("unsigned")) comparator_1 (
    .a(4'b0101), .b(inp), .eq(comparator_1_eq), .lt(comparator_1_lt));  // open: gt
  or or_1 (or_1_out, comparator_1_eq, comparator_1_lt);
  Multiplexer #(.width(4)) multiplexer_1 (.in0(inp), .in1(adder_1_out), .out(out), .sel(or_1_out));  // open: en
endmodule

module pause (
  input  [31:0] _14_y,
  input  [31:0] _15_y,
  input  [31:0] _13_y,
  input  [31:0] _16_y,
  input  [31:0] _18_y,
  input  [31:0] _17_y,
  output is_0_up
);

  wire not_1_out, not_2_out, not_3_out, not_4_out, not_5_out, not_6_out, y_down_13, y_down_14, y_down_15,
       y_down_16, y_down_17, y_down_18, y_up_13, y_up_14, y_up_15, y_up_16, y_up_17, y_up_18;

  or or_1 (y_down_14, _14_y[0], _14_y[1], _14_y[2], _14_y[3], _14_y[4], _14_y[5], _14_y[6], _14_y[7], _14_y[8], _14_y[9], _14_y[10], _14_y[11], _14_y[12], _14_y[13], _14_y[14], _14_y[15]);
  or or_2 (y_up_14, _14_y[16], _14_y[17], _14_y[18], _14_y[19], _14_y[20], _14_y[21], _14_y[22], _14_y[23], _14_y[24], _14_y[25], _14_y[26], _14_y[27], _14_y[28], _14_y[29], _14_y[30], _14_y[31]);
  or or_3 (y_down_15, _15_y[0], _15_y[1], _15_y[2], _15_y[3], _15_y[4], _15_y[5], _15_y[6], _15_y[7], _15_y[8], _15_y[9], _15_y[10], _15_y[11], _15_y[12], _15_y[13], _15_y[14], _15_y[15]);
  or or_4 (y_up_15, _15_y[16], _15_y[17], _15_y[18], _15_y[19], _15_y[20], _15_y[21], _15_y[22], _15_y[23], _15_y[24], _15_y[25], _15_y[26], _15_y[27], _15_y[28], _15_y[29], _15_y[30], _15_y[31]);
  or or_5 (y_down_16, _16_y[0], _16_y[1], _16_y[2], _16_y[3], _16_y[4], _16_y[5], _16_y[6], _16_y[7], _16_y[8], _16_y[9], _16_y[10], _16_y[11], _16_y[12], _16_y[13], _16_y[14], _16_y[15]);
  or or_6 (y_up_16, _16_y[16], _16_y[17], _16_y[18], _16_y[19], _16_y[20], _16_y[21], _16_y[22], _16_y[23], _16_y[24], _16_y[25], _16_y[26], _16_y[27], _16_y[28], _16_y[29], _16_y[30], _16_y[31]);
  or or_7 (y_down_17, _17_y[0], _17_y[1], _17_y[2], _17_y[3], _17_y[4], _17_y[5], _17_y[6], _17_y[7], _17_y[8], _17_y[9], _17_y[10], _17_y[11], _17_y[12], _17_y[13], _17_y[14], _17_y[15]);
  or or_8 (y_up_17, _17_y[16], _17_y[17], _17_y[18], _17_y[19], _17_y[20], _17_y[21], _17_y[22], _17_y[23], _17_y[24], _17_y[25], _17_y[26], _17_y[27], _17_y[28], _17_y[29], _17_y[30], _17_y[31]);
  not not_1 (not_1_out, y_up_13);
  not not_2 (not_2_out, y_up_15);
  not not_3 (not_3_out, y_up_16);
  not not_4 (not_4_out, y_up_18);
  not not_5 (not_5_out, y_up_14);
  not not_6 (not_6_out, y_up_17);
  and and_1 (is_0_up, not_1_out, not_5_out, not_2_out, not_3_out, not_6_out, not_4_out);
  or or_9 (y_down_13, _13_y[0], _13_y[1], _13_y[2], _13_y[3], _13_y[4], _13_y[5], _13_y[6], _13_y[7], _13_y[8], _13_y[9], _13_y[10], _13_y[11], _13_y[12], _13_y[13], _13_y[14], _13_y[15]);
  or or_10 (y_up_13, _13_y[16], _13_y[17], _13_y[18], _13_y[19], _13_y[20], _13_y[21], _13_y[22], _13_y[23], _13_y[24], _13_y[25], _13_y[26], _13_y[27], _13_y[28], _13_y[29], _13_y[30], _13_y[31]);
  or or_11 (y_down_18, _18_y[0], _18_y[1], _18_y[2], _18_y[3], _18_y[4], _18_y[5], _18_y[6], _18_y[7], _18_y[8], _18_y[9], _18_y[10], _18_y[11], _18_y[12], _18_y[13], _18_y[14], _18_y[15]);
  or or_12 (y_up_18, _18_y[16], _18_y[17], _18_y[18], _18_y[19], _18_y[20], _18_y[21], _18_y[22], _18_y[23], _18_y[24], _18_y[25], _18_y[26], _18_y[27], _18_y[28], _18_y[29], _18_y[30], _18_y[31]);

  // Notes on the sheet:
  //   можно ставить сверху
endmodule

module start_screen (
);

  DotMatrix #(.matrixcols(32), .matrixrows(32)) dotmatrix_1 (
    .col0({32{1'b0}}), .col1({32{1'b0}}), .col2({32{1'b0}}), .col3({32{1'b0}}), .col4(32'hfe3200),
    .col5(32'h904900), .col6(32'h904900), .col7(32'h602600), .col8({32{1'b0}}), .col9(32'hfe7f00),
    .col10(32'h904800), .col11(32'h904800), .col12(32'h6e3000), .col13({32{1'b0}}), .col14(32'hfe3f00),
    .col15(32'h924400), .col16(32'h924400), .col17(32'h923f00), .col18({32{1'b0}}), .col19(32'h641c00),
    .col20(32'h922200), .col21(32'h924100), .col22(32'h4c4100), .col23({32{1'b0}}), .col24(32'h647f00),
    .col25(32'h924900), .col26(32'h924900), .col27(32'h4c4900), .col28({32{1'b0}}), .col29({32{1'b0}}),
    .col30({32{1'b0}}), .col31({32{1'b0}}));
  // Probe on nothing
endmodule

module parse_output (
);

  wire d_ff_1_q, d_ff_2_q, isDown, power, register_2_q, register_4_q;
  wire [4:0] bit_extender_2_out, counter_1_q, dmx_x_cord;
  wire [7:0] adder_1_out, adder_2_out, divider_1_out, divider_2_out, multiplexer_1_out, multiplexer_2_out,
       multiplexer_3_out, multiplexer_4_out, register_1_q, register_3_q, subtractor_1_out, subtractor_2_out;
  wire [31:0] decoder_1_out0, decoder_3_out0, demultiplexer_1_out0, demultiplexer_1_out1,
       demultiplexer_1_out2, demultiplexer_1_out3, demultiplexer_1_out4, demultiplexer_1_out5,
       demultiplexer_1_out6, demultiplexer_1_out7, demultiplexer_1_out8, demultiplexer_1_out9,
       demultiplexer_1_out10, demultiplexer_1_out11, demultiplexer_1_out12, demultiplexer_1_out13,
       demultiplexer_1_out14, demultiplexer_1_out15, demultiplexer_1_out16, demultiplexer_1_out17,
       demultiplexer_1_out18, demultiplexer_1_out19, demultiplexer_1_out20, demultiplexer_1_out21,
       demultiplexer_1_out22, demultiplexer_1_out23, demultiplexer_1_out24, demultiplexer_1_out25,
       demultiplexer_1_out26, demultiplexer_1_out27, demultiplexer_1_out28, demultiplexer_1_out29,
       demultiplexer_1_out30, demultiplexer_1_out31, dmx_y_cord;

  Clock clock_1 (.out(power));
  D_Flip_Flop d_ff_1 (.Q(d_ff_1_q), .preset(decoder_1_out0[31]), .reset(decoder_1_out0[0]));  // open: clk, D, Qn, en
  Register register_1 (.D(multiplexer_2_out), .Q(register_1_q), .clk(power));  // open: en, clr
  DotMatrix #(.matrixcols(32), .matrixrows(32)) dotmatrix_1 (
    .col0(demultiplexer_1_out0), .col1(demultiplexer_1_out1), .col2(demultiplexer_1_out2),
    .col3(demultiplexer_1_out3), .col4(demultiplexer_1_out4), .col5(demultiplexer_1_out5),
    .col6(demultiplexer_1_out6), .col7(demultiplexer_1_out7), .col8(demultiplexer_1_out8),
    .col9(demultiplexer_1_out9), .col10(demultiplexer_1_out10), .col11(demultiplexer_1_out11),
    .col12(demultiplexer_1_out12), .col13(demultiplexer_1_out13), .col14(demultiplexer_1_out14),
    .col15(demultiplexer_1_out15), .col16(demultiplexer_1_out16), .col17(demultiplexer_1_out17),
    .col18(demultiplexer_1_out18), .col19(demultiplexer_1_out19), .col20(demultiplexer_1_out20),
    .col21(demultiplexer_1_out21), .col22(demultiplexer_1_out22), .col23(demultiplexer_1_out23),
    .col24(demultiplexer_1_out24), .col25(demultiplexer_1_out25), .col26(demultiplexer_1_out26),
    .col27(demultiplexer_1_out27), .col28(demultiplexer_1_out28), .col29(demultiplexer_1_out29),
    .col30(demultiplexer_1_out30), .col31(demultiplexer_1_out31));
  Multiplexer #(.select(3), .width(8)) multiplexer_1 (
    .in0(8'h1), .in1(8'h2), .in2(8'h4), .in3(8'h4), .in4(8'h8), .out(multiplexer_1_out), .sel(3'b000));  // open: in5, in6, in7, en
  Demultiplexer #(.select(5), .width(32)) demultiplexer_1 (
    .out0(demultiplexer_1_out0), .out1(demultiplexer_1_out1), .out2(demultiplexer_1_out2),
    .out3(demultiplexer_1_out3), .out4(demultiplexer_1_out4), .out5(demultiplexer_1_out5),
    .out6(demultiplexer_1_out6), .out7(demultiplexer_1_out7), .out8(demultiplexer_1_out8),
    .out9(demultiplexer_1_out9), .out10(demultiplexer_1_out10), .out11(demultiplexer_1_out11),
    .out12(demultiplexer_1_out12), .out13(demultiplexer_1_out13), .out14(demultiplexer_1_out14),
    .out15(demultiplexer_1_out15), .out16(demultiplexer_1_out16), .out17(demultiplexer_1_out17),
    .out18(demultiplexer_1_out18), .out19(demultiplexer_1_out19), .out20(demultiplexer_1_out20),
    .out21(demultiplexer_1_out21), .out22(demultiplexer_1_out22), .out23(demultiplexer_1_out23),
    .out24(demultiplexer_1_out24), .out25(demultiplexer_1_out25), .out26(demultiplexer_1_out26),
    .out27(demultiplexer_1_out27), .out28(demultiplexer_1_out28), .out29(demultiplexer_1_out29),
    .out30(demultiplexer_1_out30), .out31(demultiplexer_1_out31), .in(dmx_y_cord), .sel(dmx_x_cord));  // open: en
  Adder adder_1 (.a(register_1_q), .b(multiplexer_1_out), .out(adder_1_out));  // open: cin, cout
  Subtractor subtractor_1 (.a(register_1_q), .b(multiplexer_1_out), .out(subtractor_1_out));  // open: bin, bout
  Multiplexer #(.width(8)) multiplexer_2 (
    .in0(adder_1_out), .in1(subtractor_1_out), .out(multiplexer_2_out), .sel(register_2_q));  // open: en
  Register #(.width(1)) register_2 (.D(d_ff_1_q), .Q(register_2_q), .clk(power));  // open: en, clr
  Divider divider_1 (.a(multiplexer_2_out), .b(8'h8), .out(divider_1_out));  // open: upper, rem
  Bit_Extender #(.out_width(5)) bit_extender_1 (.in(divider_1_out), .out(dmx_x_cord));
  D_Flip_Flop d_ff_2 (.Q(d_ff_2_q), .preset(dmx_y_cord[31]), .reset(dmx_y_cord[0]));  // open: clk, D, Qn, en
  Decoder #(.select(5)) decoder_1 (
    .out0(decoder_1_out0[0]), .out1(decoder_1_out0[1]), .out2(decoder_1_out0[2]), .out3(decoder_1_out0[3]),
    .out4(decoder_1_out0[4]), .out5(decoder_1_out0[5]), .out6(decoder_1_out0[6]), .out7(decoder_1_out0[7]),
    .out8(decoder_1_out0[8]), .out9(decoder_1_out0[9]), .out10(decoder_1_out0[10]),
    .out11(decoder_1_out0[11]), .out12(decoder_1_out0[12]), .out13(decoder_1_out0[13]),
    .out14(decoder_1_out0[14]), .out15(decoder_1_out0[15]), .out16(decoder_1_out0[16]),
    .out17(decoder_1_out0[17]), .out18(decoder_1_out0[18]), .out19(decoder_1_out0[19]),
    .out20(decoder_1_out0[20]), .out21(decoder_1_out0[21]), .out22(decoder_1_out0[22]),
    .out23(decoder_1_out0[23]), .out24(decoder_1_out0[24]), .out25(decoder_1_out0[25]),
    .out26(decoder_1_out0[26]), .out27(decoder_1_out0[27]), .out28(decoder_1_out0[28]),
    .out29(decoder_1_out0[29]), .out30(decoder_1_out0[30]), .out31(decoder_1_out0[31]), .sel(dmx_x_cord));  // open: en
  Register register_3 (.D(multiplexer_4_out), .Q(register_3_q), .clk(power));  // open: en, clr
  Multiplexer #(.select(3), .width(8)) multiplexer_3 (
    .in0(8'h8), .in1(8'h4), .in2(8'h4), .in3(8'h2), .in4(8'h1), .out(multiplexer_3_out), .sel(3'b000));  // open: in5, in6, in7, en
  Subtractor subtractor_2 (.a(register_3_q), .b(multiplexer_3_out), .out(subtractor_2_out));  // open: bin, bout
  Adder adder_2 (.a(register_3_q), .b(multiplexer_3_out), .out(adder_2_out));  // open: cin, cout
  Multiplexer #(.width(8)) multiplexer_4 (
    .in0(adder_2_out), .in1(subtractor_2_out), .out(multiplexer_4_out), .sel(register_4_q));  // open: en
  Register #(.width(1)) register_4 (.D(d_ff_2_q), .Q(register_4_q), .clk(power));  // open: en, clr
  Bit_Extender #(.out_width(5)) bit_extender_2 (.in(divider_2_out), .out(bit_extender_2_out));
  Divider divider_2 (.a(multiplexer_4_out), .b(8'h8), .out(divider_2_out));  // open: upper, rem
  Decoder #(.select(5)) decoder_2 (
    .out0(dmx_y_cord[0]), .out1(dmx_y_cord[1]), .out2(dmx_y_cord[2]), .out3(dmx_y_cord[3]),
    .out4(dmx_y_cord[4]), .out5(dmx_y_cord[5]), .out6(dmx_y_cord[6]), .out7(dmx_y_cord[7]),
    .out8(dmx_y_cord[8]), .out9(dmx_y_cord[9]), .out10(dmx_y_cord[10]), .out11(dmx_y_cord[11]),
    .out12(dmx_y_cord[12]), .out13(dmx_y_cord[13]), .out14(dmx_y_cord[14]), .out15(dmx_y_cord[15]),
    .out16(dmx_y_cord[16]), .out17(dmx_y_cord[17]), .out18(dmx_y_cord[18]), .out19(dmx_y_cord[19]),
    .out20(dmx_y_cord[20]), .out21(dmx_y_cord[21]), .out22(dmx_y_cord[22]), .out23(dmx_y_cord[23]),
    .out24(dmx_y_cord[24]), .out25(dmx_y_cord[25]), .out26(dmx_y_cord[26]), .out27(dmx_y_cord[27]),
    .out28(dmx_y_cord[28]), .out29(dmx_y_cord[29]), .out30(dmx_y_cord[30]), .out31(dmx_y_cord[31]),
    .sel(bit_extender_2_out));  // open: en
  D_Flip_Flop d_ff_3 (.Q(isDown), .preset(decoder_3_out0[31]), .reset(decoder_3_out0[0]));  // open: clk, D, Qn, en
  Counter #(.width(5), .max('h1f)) counter_1 (
    .load(isDown), .Q(counter_1_q), .clk(power));  // open: D, count, carry, clr
  Decoder #(.select(5)) decoder_3 (
    .out0(decoder_3_out0[0]), .out1(decoder_3_out0[1]), .out2(decoder_3_out0[2]), .out3(decoder_3_out0[3]),
    .out4(decoder_3_out0[4]), .out5(decoder_3_out0[5]), .out6(decoder_3_out0[6]), .out7(decoder_3_out0[7]),
    .out8(decoder_3_out0[8]), .out9(decoder_3_out0[9]), .out10(decoder_3_out0[10]),
    .out11(decoder_3_out0[11]), .out12(decoder_3_out0[12]), .out13(decoder_3_out0[13]),
    .out14(decoder_3_out0[14]), .out15(decoder_3_out0[15]), .out16(decoder_3_out0[16]),
    .out17(decoder_3_out0[17]), .out18(decoder_3_out0[18]), .out19(decoder_3_out0[19]),
    .out20(decoder_3_out0[20]), .out21(decoder_3_out0[21]), .out22(decoder_3_out0[22]),
    .out23(decoder_3_out0[23]), .out24(decoder_3_out0[24]), .out25(decoder_3_out0[25]),
    .out26(decoder_3_out0[26]), .out27(decoder_3_out0[27]), .out28(decoder_3_out0[28]),
    .out29(decoder_3_out0[29]), .out30(decoder_3_out0[30]), .out31(decoder_3_out0[31]), .sel(counter_1_q));  // open: en

  // Notes on the sheet:
  //   движение по оси x
  //   движение по оси y
  //   движение по оси x
endmodule

module stopWatch2hz (
  input  start,
  input  takt,
  input  \null ,
  output [3:0] min_1,
  output [3:0] min_0,
  output [3:0] sec_1,
  output [3:0] sec_0
);

  wire and_1_out, and_2_out, and_3_out, and_4_out, and_5_out, d_ff_1_q, frequency_divider_1_out,
       frequency_divider_11bit_1_out, not_1_out, not_2_out, not_3_out, not_4_out, not_5_out, not_6_out,
       or_1_out, or_2_out, or_3_out;

  Counter #(.width(4), .max('hf)) counter_1 (.Q(min_1), .clk(and_1_out), .clr(\null ));  // open: load, D, count, carry
  frequency_divider_11bit frequency_divider_11bit_1 (
    .IN(takt), .n(11'h330), .OUT(frequency_divider_11bit_1_out));  // open: _0
  // Probe on min_0
  Counter #(.width(4), .max('hf)) counter_2 (
    .Q(min_0), .clk(and_4_out), .clr(or_1_out));  // open: load, D, count, carry
  or or_1 (or_1_out, \null , and_1_out);
  frequency_divider frequency_divider_1 (
    .IN(frequency_divider_11bit_1_out), .OUT(frequency_divider_1_out), .n(8'h2));  // open: _0
  D_Flip_Flop d_ff_1 (.Q(d_ff_1_q), .preset(frequency_divider_1_out));  // open: clk, D, Qn, en, reset
  not not_1 (not_1_out, min_0[0]);
  not not_2 (not_2_out, min_0[2]);
  and and_1 (and_1_out, not_1_out, min_0[1], not_2_out, min_0[3]);
  // Probe on sec_1
  Counter #(.width(4), .max('hf)) counter_3 (
    .Q(sec_1), .clk(and_5_out), .clr(or_2_out));  // open: load, D, count, carry
  or or_2 (or_2_out, \null , and_4_out);
  and and_2 (and_2_out, start, d_ff_1_q);
  and and_3 (and_3_out, and_2_out, frequency_divider_11bit_1_out);
  Hex_Digit_Display hex_digit_display_1 (.value(min_1));  // open: dp
  Hex_Digit_Display hex_digit_display_2 (.value(min_0));  // open: dp
  not not_3 (not_3_out, sec_1[0]);
  not not_4 (not_4_out, sec_1[3]);
  Hex_Digit_Display hex_digit_display_3 (.value(sec_1));  // open: dp
  and and_4 (and_4_out, not_3_out, sec_1[1], sec_1[2], not_4_out);
  Counter #(.width(4), .max('hf)) counter_4 (
    .Q(sec_0), .clk(and_3_out), .clr(or_3_out));  // open: load, D, count, carry
  or or_3 (or_3_out, \null , and_5_out);
  Hex_Digit_Display hex_digit_display_4 (.value(sec_0));  // open: dp
  // Probe on sec_0
  not not_5 (not_5_out, sec_0[0]);
  not not_6 (not_6_out, sec_0[2]);
  and and_5 (and_5_out, not_5_out, sec_0[1], not_6_out, sec_0[3]);
endmodule

module frequency_divider_11bit (
  input  [10:0] n,
  input  IN,
  input  _0,
  output OUT
);

  wire comparator_1_eq, comparator_1_lt, or_1_out, or_2_out;
  wire [10:0] counter_1_q;

  Counter #(.width(11), .max('h7ff)) counter_1 (
    .count(IN), .Q(counter_1_q), .clk(IN), .clr(or_1_out));  // open: load, D, carry
  or or_1 (or_1_out, _0, or_2_out);
  Comparator #(.width(11), .mode("unsigned")) comparator_1 (
    .a(n), .b(counter_1_q), .eq(comparator_1_eq), .lt(comparator_1_lt));  // open: gt
  or or_2 (or_2_out, comparator_1_eq, comparator_1_lt);
  T_Flip_Flop t_ff_1 (.clk(or_2_out), .T(or_2_out), .Q(OUT), .reset(_0));  // open: Qn, preset, en
endmodule

module PING_PONG (
);

  wire movepoint_1_keyboard_power;
  wire [3:0] movepoint_1_min_0, movepoint_1_min_1, movepoint_1_out_2, movepoint_1_out_3, movepoint_1_out_4,
       movepoint_1_out_37, movepoint_1_out_38, movepoint_1_out_39, movepoint_1_sec_0, movepoint_1_sec_1;
  wire [6:0] keyboard_1_data;
  wire [31:0] movepoint_1_out_5, movepoint_1_out_6, movepoint_1_out_7, movepoint_1_out_8, movepoint_1_out_9,
       movepoint_1_out_10, movepoint_1_out_11, movepoint_1_out_12, movepoint_1_out_13, movepoint_1_out_14,
       movepoint_1_out_15, movepoint_1_out_16, movepoint_1_out_17, movepoint_1_out_18, movepoint_1_out_19,
       movepoint_1_out_20, movepoint_1_out_21, movepoint_1_out_22, movepoint_1_out_23, movepoint_1_out_24,
       movepoint_1_out_25, movepoint_1_out_26, movepoint_1_out_27, movepoint_1_out_28, movepoint_1_out_29,
       movepoint_1_out_30, movepoint_1_out_31, movepoint_1_out_32, movepoint_1_out_33, movepoint_1_out_34,
       movepoint_1_out_35, movepoint_1_out_36;

  Hex_Digit_Display hex_digit_display_1 (.value(movepoint_1_out_2));  // open: dp
  Hex_Digit_Display hex_digit_display_2 (.value(movepoint_1_out_3));  // open: dp
  movePoint movepoint_1 (
    .out_5(movepoint_1_out_5), .out_6(movepoint_1_out_6), .out_7(movepoint_1_out_7),
    .out_8(movepoint_1_out_8), .out_9(movepoint_1_out_9), .out_10(movepoint_1_out_10),
    .out_11(movepoint_1_out_11), .out_12(movepoint_1_out_12), .out_13(movepoint_1_out_13),
    .out_14(movepoint_1_out_14), .out_15(movepoint_1_out_15), .out_16(movepoint_1_out_16),
    .out_17(movepoint_1_out_17), .out_18(movepoint_1_out_18), .out_19(movepoint_1_out_19),
    .out_20(movepoint_1_out_20), .out_21(movepoint_1_out_21), .out_22(movepoint_1_out_22),
    .out_23(movepoint_1_out_23), .out_24(movepoint_1_out_24), .out_25(movepoint_1_out_25),
    .out_26(movepoint_1_out_26), .out_27(movepoint_1_out_27), .out_28(movepoint_1_out_28),
    .out_29(movepoint_1_out_29), .out_30(movepoint_1_out_30), .out_31(movepoint_1_out_31),
    .out_32(movepoint_1_out_32), .out_33(movepoint_1_out_33), .Keyboard(keyboard_1_data),
    .out_34(movepoint_1_out_34), .out_35(movepoint_1_out_35), .out_36(movepoint_1_out_36),
    .keyboard_power(movepoint_1_keyboard_power), .out_4(movepoint_1_out_4), .out_3(movepoint_1_out_3),
    .out_2(movepoint_1_out_2), .out_39(movepoint_1_out_39), .out_38(movepoint_1_out_38),
    .out_37(movepoint_1_out_37), .min_1(movepoint_1_min_1), .min_0(movepoint_1_min_0),
    .sec_1(movepoint_1_sec_1), .sec_0(movepoint_1_sec_0));
  Hex_Digit_Display hex_digit_display_3 (.value(movepoint_1_out_4));  // open: dp
  DotMatrix #(.matrixcols(32), .matrixrows(32)) dotmatrix_1 (
    .col0(movepoint_1_out_5), .col1(movepoint_1_out_6), .col2(movepoint_1_out_7), .col3(movepoint_1_out_8),
    .col4(movepoint_1_out_9), .col5(movepoint_1_out_10), .col6(movepoint_1_out_11),
    .col7(movepoint_1_out_12), .col8(movepoint_1_out_13), .col9(movepoint_1_out_14),
    .col10(movepoint_1_out_15), .col11(movepoint_1_out_16), .col12(movepoint_1_out_17),
    .col13(movepoint_1_out_18), .col14(movepoint_1_out_19), .col15(movepoint_1_out_20),
    .col16(movepoint_1_out_21), .col17(movepoint_1_out_22), .col18(movepoint_1_out_23),
    .col19(movepoint_1_out_24), .col20(movepoint_1_out_25), .col21(movepoint_1_out_26),
    .col22(movepoint_1_out_27), .col23(movepoint_1_out_28), .col24(movepoint_1_out_29),
    .col25(movepoint_1_out_30), .col26(movepoint_1_out_31), .col27(movepoint_1_out_32),
    .col28(movepoint_1_out_33), .col29(movepoint_1_out_34), .col30(movepoint_1_out_35),
    .col31(movepoint_1_out_36));
  Hex_Digit_Display hex_digit_display_4 (.value(movepoint_1_min_1));  // open: dp
  Keyboard keyboard_1 (.clk(movepoint_1_keyboard_power), .data(keyboard_1_data));  // open: re, clr, avail
  Hex_Digit_Display hex_digit_display_5 (.value(movepoint_1_min_0));  // open: dp
  Hex_Digit_Display hex_digit_display_6 (.value(movepoint_1_sec_1));  // open: dp
  Hex_Digit_Display hex_digit_display_7 (.value(movepoint_1_sec_0));  // open: dp
  Hex_Digit_Display hex_digit_display_8 (.value(movepoint_1_out_37));  // open: dp
  Hex_Digit_Display hex_digit_display_9 (.value(movepoint_1_out_38));  // open: dp
  Hex_Digit_Display hex_digit_display_10 (.value(movepoint_1_out_39));  // open: dp

  // Notes on the sheet:
  //   Player 1 - W and S
  //   Player 2 - O and L
  //   Pause - P
  //   Restart - R
  //   Bot - B
  //   Start game - SPACE
endmodule

module bot_borris (
  input  [7:0] X,
  input  [7:0] Y,
  input  [7:0] Vx,
  input  [7:0] Vy,
  output [7:0] New_Y
);

  wire cdm_8_mark5_1_p1, cdm_8_mark5_1_p2, cdm_8_mark5_1_p4, cdm_8_mark5_1_p5, cdm_8_mark5_1_p6,
       cdm_8_mark5_1_p7, cdm_8_mark5_1_p8, cdm_8_mark5_1_p9, cdm_8_mark5_1_p10, clk, code, data,
       decoder_2_out0, decoder_2_out1, \inout , IOsel, nand_1_out, not_1_out, not_2_out, not_4_out, RAM,
       undriven_2;
  wire [3:0] IOaddr, not_3_out;
  wire [7:0] cdm_8_mark5_1_p13, cdm_8_mark5_1_p14, controlled_buffer_5_out, controlled_buffer_6_out, IOdat,
       multiplexer_1_out, undriven;
  wire [7:4] cdm_8_mark5_1_p12;

  Clock clock_1 (.out(clk));
  // Probe on cdm_8_mark5_1_p1
  // Probe on cdm_8_mark5_1_p5
  // Probe on cdm_8_mark5_1_p4
  // Probe on cdm_8_mark5_1_p2
  // Probe on cdm_8_mark5_1_p6
  // Probe on cdm_8_mark5_1_p7
  // Probe on cdm_8_mark5_1_p8
  // CdM_8_mark5 cdm_8_mark5_1: pin names not known; wires that end beside it: cdm_8_mark5_1_p1, cdm_8_mark5_1_p2, clk, cdm_8_mark5_1_p4, cdm_8_mark5_1_p5, cdm_8_mark5_1_p6, cdm_8_mark5_1_p7, cdm_8_mark5_1_p8, cdm_8_mark5_1_p9, cdm_8_mark5_1_p10, \inout , {cdm_8_mark5_1_p12, IOaddr}, cdm_8_mark5_1_p13, cdm_8_mark5_1_p14, {cdm_8_mark5_1_p12, IOaddr}
  not not_1 (not_1_out, \inout );
  assign cdm_8_mark5_1_p14 = \inout  ? IOdat : 8'bz;  // Controlled_Buffer controlled_buffer_1
  and and_1 (IOsel, not_2_out, clk, data);
  Decoder #(.disabled(0)) decoder_1 (.out0(code), .out1(data), .sel(cdm_8_mark5_1_p9), .en(cdm_8_mark5_1_p10));
  assign IOdat = not_1_out ? cdm_8_mark5_1_p13 : 8'bz;  // Controlled_Buffer controlled_buffer_2
  not not_2 (not_2_out, nand_1_out);
  and and_2 (RAM, nand_1_out, data);
  nand nand_1 (nand_1_out, cdm_8_mark5_1_p12[4], cdm_8_mark5_1_p12[5], cdm_8_mark5_1_p12[6], cdm_8_mark5_1_p12[7]);
  // Probe on IOdat
  ROM rom_1 (.addr({cdm_8_mark5_1_p12, IOaddr}), .data(IOdat), .sel(code));
  RAM ram_1 (.addr({cdm_8_mark5_1_p12, IOaddr}), .data(IOdat), .sel(RAM), .clk(clk), .ld(\inout ));  // open: clr
  Multiplexer #(.select(2), .width(8), .disabled(0)) multiplexer_1 (
    .in0(X), .in1(Y), .in2(Vx), .in3(Vy), .out(multiplexer_1_out), .sel(IOaddr[1:0]));  // open: en
  // Probe on multiplexer_1_out
  assign New_Y = decoder_2_out0 ? IOdat : 8'bz;  // Controlled_Buffer controlled_buffer_3
  assign IOdat = decoder_2_out1 ? multiplexer_1_out : 8'bz;  // Controlled_Buffer controlled_buffer_4
  Pull_Resistor pull_resistor_1 (.node(New_Y));
  // AND_Gate and_3 has open pins: in0=IOsel, in1=not_3_out[0], in2=not_3_out[1], in3=not_3_out[2], in4=not_3_out[3], out=open
  Decoder #(.disabled(0)) decoder_2 (.out0(decoder_2_out0), .out1(decoder_2_out1), .sel(\inout ), .en(IOsel));
  assign not_3_out = ~IOaddr;  // NOT_Gate not_3, 4 bits wide
  assign controlled_buffer_5_out = undriven_2 ? controlled_buffer_6_out : 8'bz;  // Controlled_Buffer controlled_buffer_5
  not not_4 (not_4_out, undriven_2);
  assign controlled_buffer_6_out = not_4_out ? undriven : 8'bz;  // Controlled_Buffer controlled_buffer_6

  // Other names for the same wires on the sheet: rdwr = \inout 

  // Notes on the sheet:
  //   or
  //   Y = (Sy + Vy * (Sx / Vx)) % 32
  //   D0F0B105ED06D000A1D0F1B105ED0FD001A1D0F2B105ED18D002A1D0F3B105ED21D003A1D200D000B0D102B571ED398514858EEE308ED001B0D103B58AE04614EE4014202020909090D1F4A4EE04
  //   contents of rom_1 (hex, n*v repeats v):
  //   4*0 d0 f0 b1 5 ed 6 d0 0 a1 d0 f1 b1 5 ed f d0 1 a1 d0 f2 b1 5 ed 18 d0 2 a1 d0 f3 b1 5 ed 21 d0 e0
  //   5 e5 2f 85 d2 1 ee 31 d2 0 a2 d0 3 a1 d2 0 d0 0 b0 d1 3 b5 a e4 44 15 86 ee 3d d0 2 b0 d3 0 74 e0 52
  //   8f 84 11 84 ee 49 8f d0 1 b0 d1 e0 b5 5 e0 5d 87 1c 0 e5 66 84 d1 1 ee 68 d1 0 b5 4*94 d2 e1 0 e3 76
  //   d2 1 ee 78 d2 0 ba 4*90 5 e1 89 a e0 87 d3 e0 1c 84 ee 90 a e1 90 d3 e0 1c 84 d1 f4 a4 ee 4 105*0 1c
  //   AS OF RIGHT NOW: X, Y, Vx, Vy -- cannot be 0
  //   new Y: 0xf4
  //   NOTE: bc all the div and mul are coded as while loops -- the X coord must be greater than the Vx speed
  //   X: 0xf0
  //   Y: 0xf1
  //   Vx: 0xf2
  //   Vy: 0xf3
  //   write
  //   read
  //   for testing
endmodule

module last_button_press (
  input  button,
  input  opposite_button,
  input  power,
  output button_pressed
);

  wire frequency_divider_1_out, or_1_out, or_2_out;

  frequency_divider frequency_divider_1 (.IN(power), .OUT(frequency_divider_1_out), .n({8{1'b1}}), ._0(or_1_out));
  or or_1 (or_1_out, button, frequency_divider_1_out);
  D_Flip_Flop d_ff_1 (.clk(button), .D(button), .Q(button_pressed), .reset(or_2_out));  // open: Qn, preset, en
  or or_2 (or_2_out, frequency_divider_1_out, opposite_button);
endmodule

module win_lose_screen (
);

  DotMatrix #(.matrixcols(32), .matrixrows(32)) dotmatrix_1 (
    .col0({32{1'b0}}), .col1({32{1'b0}}), .col2({32{1'b0}}), .col3({32{1'b0}}), .col4(32'h60000),
    .col5(32'h90000), .col6(32'h9c000), .col7(32'h63000), .col8(32'h10c00), .col9(32'h10200),
    .col10(32'h8200), .col11(32'h8200), .col12(32'h4200), .col13(32'h18200), .col14(32'h360200),
    .col15(32'h480200), .col16(32'h480200), .col17(32'h360200), .col18(32'h18200), .col19(32'h4200),
    .col20(32'h8200), .col21(32'h8200), .col22(32'h10200), .col23(32'h10c00), .col24(32'h63000),
    .col25(32'h9c000), .col26(32'h90000), .col27(32'h60000), .col28({32{1'b0}}), .col29({32{1'b0}}),
    .col30({32{1'b0}}), .col31({32{1'b0}}));
  DotMatrix #(.matrixcols(32), .matrixrows(32)) dotmatrix_2 (
    .col0({32{1'b0}}), .col1({32{1'b0}}), .col2({32{1'b0}}), .col3({32{1'b0}}), .col4({32{1'b0}}),
    .col5({32{1'b0}}), .col6({32{1'b0}}), .col7({32{1'b0}}), .col8(32'h7c000), .col9(32'h382000),
    .col10(32'h439000), .col11(32'h87d000), .col12(32'h87cf00), .col13(32'h107c080), .col14(32'h1038080),
    .col15(32'h1001880), .col16(32'h1001880), .col17(32'h1038080), .col18(32'h107c080), .col19(32'h87cf00),
    .col20(32'h87d000), .col21(32'h439000), .col22(32'h382000), .col23(32'h7c000), .col24({32{1'b0}}),
    .col25({32{1'b0}}), .col26({32{1'b0}}), .col27({32{1'b0}}), .col28({32{1'b0}}), .col29({32{1'b0}}),
    .col30({32{1'b0}}), .col31({32{1'b0}}));
endmodule

module goto_y (
  input  [31:0] cur_racket,
  input  [31:0] predict,
  output [31:0] \output 
);

  wire comparator_1_lt, comparator_2_eq;
  wire [31:0] multiplexer_1_out, shifter_1_out, shifter_2_out;

  Shifter #(.width(32), .shift("lr")) shifter_1 (.in(cur_racket), .\dist (5'b00001), .out(shifter_1_out));
  Shifter #(.width(32)) shifter_2 (.in(cur_racket), .\dist (5'b00001), .out(shifter_2_out));
  Comparator #(.width(32)) comparator_1 (.a(cur_racket), .b(predict), .lt(comparator_1_lt));  // open: gt, eq
  Comparator #(.width(32)) comparator_2 (.a(cur_racket), .b(predict), .eq(comparator_2_eq));  // open: gt, lt
  Multiplexer #(.width(32)) multiplexer_1 (
    .in0(shifter_1_out), .in1(shifter_2_out), .out(multiplexer_1_out), .sel(comparator_1_lt));  // open: en
  Multiplexer #(.width(32)) multiplexer_2 (
    .in0(multiplexer_1_out), .in1(cur_racket), .out(\output ), .sel(comparator_2_eq));  // open: en

  // Other names for the same wires on the sheet: pred_y[31:0] = predict; racket_y[31:0] = cur_racket
endmodule
