// Logisim project stopwatch2Hz.circ as structural Verilog: 1 circuit, main circuit mt_clock
module mt_clock (
);

  wire and_1_out, and_2_out, and_3_out, clock_1_out, not_1_out, not_2_out, not_3_out, not_4_out, not_5_out,
       not_6_out;
  wire [3:0] counter_1_q, counter_2_q, counter_3_q, counter_4_q;

  Counter #(.width(4), .max('hf)) counter_1 (.Q(counter_1_q), .clk(and_1_out));  // open: load, D, count, carry, clr
  Clock clock_1 (.out(clock_1_out));
  // Probe on counter_2_q
  Counter #(.width(4), .max('hf)) counter_2 (
    .Q(counter_2_q), .clk(and_2_out), .clr(and_1_out));  // open: load, D, count, carry
  not not_1 (not_1_out, counter_2_q[0]);
  not not_2 (not_2_out, counter_2_q[2]);
  and and_1 (and_1_out, not_1_out, counter_2_q[1], not_2_out, counter_2_q[3]);
  // Probe on counter_3_q
  Counter #(.width(4), .max('hf)) counter_3 (
    .Q(counter_3_q), .clk(and_3_out), .clr(and_2_out));  // open: load, D, count, carry
  Hex_Digit_Display hex_digit_display_1 (.value(counter_1_q));  // open: dp
  Hex_Digit_Display hex_digit_display_2 (.value(counter_2_q));  // open: dp
  not not_3 (not_3_out, counter_3_q[0]);
  not not_4 (not_4_out, counter_3_q[3]);
  Hex_Digit_Display hex_digit_display_3 (.value(counter_3_q));  // open: dp
  and and_2 (and_2_out, not_3_out, counter_3_q[1], counter_3_q[2], not_4_out);
  Counter #(.width(4), .max('hf)) counter_4 (
    .Q(counter_4_q), .clk(clock_1_out), .clr(and_3_out));  // open: load, D, count, carry
  Hex_Digit_Display hex_digit_display_4 (.value(counter_4_q));  // open: dp
  // Probe on counter_4_q
  not not_5 (not_5_out, counter_4_q[0]);
  not not_6 (not_6_out, counter_4_q[2]);
  and and_3 (and_3_out, not_5_out, counter_4_q[1], not_6_out, counter_4_q[3]);
endmodule
