// Logisim project updated-movement-beta2.circ as structural Verilog: 1 circuit, main circuit main
module main (
);

  wire adder_1_cout, adder_2_cout, adder_3_cout, adder_4_cout, and_1_out, and_2_out, clock_1_out,
       clock_2_out, not_1_out, not_2_out, not_3_out, not_4_out, or_1_out, or_2_out, register_1_q,
       register_2_q, subtractor_1_bout, subtractor_2_bout, t_ff_1_q, t_ff_2_q;
  wire [2:0] register_3_q, register_4_q;
  wire [4:0] adder_3_out, adder_4_out, bit_extender_1_out, bit_extender_2_out, dmx_x_cord, multiplexer_7_out,
       multiplexer_8_out, register_4_q_2;
  wire [7:0] adder_1_out, adder_2_out, multiplexer_1_out, multiplexer_2_out, multiplexer_3_out,
       multiplexer_4_out, multiplexer_5_out, multiplexer_6_out, subtractor_1_out, subtractor_2_out,
       subtractor_3_out, subtractor_4_out, subtractor_5_out, subtractor_6_out, subtractor_7_out,
       subtractor_8_out;
  wire [31:0] demultiplexer_1_out0, demultiplexer_1_out1, demultiplexer_1_out2, demultiplexer_1_out3,
       demultiplexer_1_out4, demultiplexer_1_out5, demultiplexer_1_out6, demultiplexer_1_out7,
       demultiplexer_1_out8, demultiplexer_1_out9, demultiplexer_1_out10, demultiplexer_1_out11,
       demultiplexer_1_out12, demultiplexer_1_out13, demultiplexer_1_out14, demultiplexer_1_out15,
       demultiplexer_1_out16, demultiplexer_1_out17, demultiplexer_1_out18, demultiplexer_1_out19,
       demultiplexer_1_out20, demultiplexer_1_out21, demultiplexer_1_out22, demultiplexer_1_out23,
       demultiplexer_1_out24, demultiplexer_1_out25, demultiplexer_1_out26, demultiplexer_1_out27,
       demultiplexer_1_out28, demultiplexer_1_out29, demultiplexer_1_out30, demultiplexer_1_out31, dmx_y_cord;

  DotMatrix #(.matrixcols(32), .matrixrows(32)) dotmatrix_1 (
    .col0(demultiplexer_1_out0), .col1(demultiplexer_1_out1), .col2(demultiplexer_1_out2),
    .col3(demultiplexer_1_out3), .col4(demultiplexer_1_out4), .col5(demultiplexer_1_out5),
    .col6(demultiplexer_1_out6), .col7(demultiplexer_1_out7), .col8(demultiplexer_1_out8),
    .col9(demultiplexer_1_out9), .col10(demultiplexer_1_out10), .col11(demultiplexer_1_out11),
    .col12(demultiplexer_1_out12), .col13(demultiplexer_1_out13), .col14(demultiplexer_1_out14),
    .col15(demultiplexer_1_out15), .col16(demultiplexer_1_out16), .col17(demultiplexer_1_out17),
    .col18(demultiplexer_1_out18), .col19(demultiplexer_1_out19), .col20(demultiplexer_1_out20),
    .col21(demultiplexer_1_out21), .col22(demultiplexer_1_out22), .col23(demultiplexer_1_out23),
    .col24(demultiplexer_1_out24), .col25(demultiplexer_1_out25), .col26(demultiplexer_1_out26),
    .col27(demultiplexer_1_out27), .col28(demultiplexer_1_out28), .col29(demultiplexer_1_out29),
    .col30(demultiplexer_1_out30), .col31(demultiplexer_1_out31));
  Demultiplexer #(.select(5), .width(32)) demultiplexer_1 (
    .out0(demultiplexer_1_out0), .out1(demultiplexer_1_out1), .out2(demultiplexer_1_out2),
    .out3(demultiplexer_1_out3), .out4(demultiplexer_1_out4), .out5(demultiplexer_1_out5),
    .out6(demultiplexer_1_out6), .out7(demultiplexer_1_out7), .out8(demultiplexer_1_out8),
    .out9(demultiplexer_1_out9), .out10(demultiplexer_1_out10), .out11(demultiplexer_1_out11),
    .out12(demultiplexer_1_out12), .out13(demultiplexer_1_out13), .out14(demultiplexer_1_out14),
    .out15(demultiplexer_1_out15), .out16(demultiplexer_1_out16), .out17(demultiplexer_1_out17),
    .out18(demultiplexer_1_out18), .out19(demultiplexer_1_out19), .out20(demultiplexer_1_out20),
    .out21(demultiplexer_1_out21), .out22(demultiplexer_1_out22), .out23(demultiplexer_1_out23),
    .out24(demultiplexer_1_out24), .out25(demultiplexer_1_out25), .out26(demultiplexer_1_out26),
    .out27(demultiplexer_1_out27), .out28(demultiplexer_1_out28), .out29(demultiplexer_1_out29),
    .out30(demultiplexer_1_out30), .out31(demultiplexer_1_out31), .in(dmx_y_cord), .sel(dmx_x_cord));  // open: en
  Multiplexer #(.width(8)) multiplexer_1 (
    .in0({dmx_x_cord, register_3_q}), .in1(subtractor_6_out), .out(multiplexer_1_out), .sel(and_1_out));  // open: en
  Multiplexer #(.width(8)) multiplexer_2 (
    .in0({register_4_q_2, register_4_q}), .in1(subtractor_8_out), .out(multiplexer_2_out), .sel(and_2_out));  // open: en
  Multiplexer #(.width(8)) multiplexer_3 (
    .in0(8'h8), .in1(subtractor_5_out), .out(multiplexer_3_out), .sel(adder_2_cout));  // open: en
  and and_1 (and_1_out, register_1_q, not_1_out);
  not not_1 (not_1_out, t_ff_2_q);
  Subtractor subtractor_1 (
    .a({register_4_q_2, register_4_q}), .b(multiplexer_4_out), .out(subtractor_1_out),
    .bout(subtractor_1_bout));  // open: bin
  Multiplexer #(.width(8)) multiplexer_4 (
    .in0(8'h1), .in1(subtractor_7_out), .out(multiplexer_4_out), .sel(adder_1_cout));  // open: en
  Adder adder_1 (.a(8'h1), .b(multiplexer_2_out), .out(adder_1_out), .cout(adder_1_cout));  // open: cin
  and and_2 (and_2_out, register_2_q, not_2_out);
  not not_2 (not_2_out, t_ff_1_q);
  Subtractor subtractor_2 (
    .a({dmx_x_cord, register_3_q}), .b(multiplexer_3_out), .out(subtractor_2_out), .bout(subtractor_2_bout));  // open: bin
  Register #(.width(1)) register_1 (
    .D(subtractor_2_bout), .Q(register_1_q), .clk(subtractor_2_bout), .clr(not_3_out));  // open: en
  not not_3 (not_3_out, clock_1_out);
  Adder adder_2 (.a(8'h8), .b(multiplexer_1_out), .out(adder_2_out), .cout(adder_2_cout));  // open: cin
  or or_1 (or_1_out, adder_2_cout, register_1_q);
  Register #(.width(1)) register_2 (
    .D(subtractor_1_bout), .Q(register_2_q), .clk(subtractor_1_bout), .clr(not_4_out));  // open: en
  not not_4 (not_4_out, clock_2_out);
  or or_2 (or_2_out, adder_1_cout, register_2_q);
  T_Flip_Flop t_ff_1 (.clk(or_2_out), .T(or_2_out), .Q(t_ff_1_q));  // open: Qn, preset, reset, en
  Multiplexer #(.width(8)) multiplexer_5 (
    .in0(adder_2_out), .in1(subtractor_2_out), .out(multiplexer_5_out), .sel(t_ff_2_q));  // open: en
  Register register_3 (.D(multiplexer_5_out), .Q({dmx_x_cord, register_3_q}), .clk(clock_1_out));  // open: en, clr
  Clock clock_1 (.out(clock_1_out));
  T_Flip_Flop t_ff_2 (.clk(or_1_out), .T(or_1_out), .Q(t_ff_2_q));  // open: Qn, preset, reset, en
  Multiplexer #(.width(8)) multiplexer_6 (
    .in0(adder_1_out), .in1(subtractor_1_out), .out(multiplexer_6_out), .sel(t_ff_1_q));  // open: en
  Register register_4 (.D(multiplexer_6_out), .Q({register_4_q_2, register_4_q}), .clk(clock_2_out));  // open: en, clr
  Clock clock_2 (.out(clock_2_out));
  Subtractor subtractor_3 (.a({8{1'b1}}), .b({dmx_x_cord, register_3_q}), .out(subtractor_3_out));  // open: bin, bout
  Subtractor subtractor_4 (
    .a({8{1'b1}}), .b({register_4_q_2, register_4_q}), .out(subtractor_4_out));  // open: bin, bout
  Subtractor subtractor_5 (.a(8'h8), .b(subtractor_3_out), .out(subtractor_5_out));  // open: bin, bout
  Subtractor subtractor_6 (.a(8'h8), .b({dmx_x_cord, register_3_q}), .out(subtractor_6_out));  // open: bin, bout
  Subtractor subtractor_7 (.a(8'h1), .b(subtractor_4_out), .out(subtractor_7_out));  // open: bin, bout
  Subtractor subtractor_8 (.a(8'h1), .b({register_4_q_2, register_4_q}), .out(subtractor_8_out));  // open: bin, bout
  // Probe on {dmx_x_cord, register_3_q}
  // Probe on {register_4_q_2, register_4_q}
  assign bit_extender_1_out = {{4{1'b0}}, register_3_q[2]};  // Bit_Extender bit_extender_1
  assign bit_extender_2_out = {{4{1'b0}}, register_4_q[2]};  // Bit_Extender bit_extender_2
  Adder #(.width(5)) adder_3 (
    .a(bit_extender_2_out), .b(register_4_q_2), .out(adder_3_out), .cout(adder_3_cout));  // open: cin
  Adder #(.width(5)) adder_4 (
    .a(bit_extender_1_out), .b(dmx_x_cord), .out(adder_4_out), .cout(adder_4_cout));  // open: cin
  Multiplexer #(.width(5)) multiplexer_7 (
    .in0(adder_4_out), .in1({5{1'b1}}), .out(multiplexer_7_out), .sel(adder_4_cout));  // open: en
  Multiplexer #(.width(5)) multiplexer_8 (
    .in0(adder_3_out), .in1({5{1'b1}}), .out(multiplexer_8_out), .sel(adder_3_cout));  // open: en
  Decoder #(.select(5)) decoder_1 (
    .out0(dmx_y_cord[0]), .out1(dmx_y_cord[1]), .out2(dmx_y_cord[2]), .out3(dmx_y_cord[3]),
    .out4(dmx_y_cord[4]), .out5(dmx_y_cord[5]), .out6(dmx_y_cord[6]), .out7(dmx_y_cord[7]),
    .out8(dmx_y_cord[8]), .out9(dmx_y_cord[9]), .out10(dmx_y_cord[10]), .out11(dmx_y_cord[11]),
    .out12(dmx_y_cord[12]), .out13(dmx_y_cord[13]), .out14(dmx_y_cord[14]), .out15(dmx_y_cord[15]),
    .out16(dmx_y_cord[16]), .out17(dmx_y_cord[17]), .out18(dmx_y_cord[18]), .out19(dmx_y_cord[19]),
    .out20(dmx_y_cord[20]), .out21(dmx_y_cord[21]), .out22(dmx_y_cord[22]), .out23(dmx_y_cord[23]),
    .out24(dmx_y_cord[24]), .out25(dmx_y_cord[25]), .out26(dmx_y_cord[26]), .out27(dmx_y_cord[27]),
    .out28(dmx_y_cord[28]), .out29(dmx_y_cord[29]), .out30(dmx_y_cord[30]), .out31(dmx_y_cord[31]),
    .sel(register_4_q_2));  // open: en

  // Notes on the sheet:
  //   Движение по X
  //   Движение по Y
  //   Скорость по Y
  //   Скорость по X
  //   Updated Movement Beta 2
  //   Скорость может быть почти любой.
  //   Аналогично с другими стенками
  //   У стенок шарик останавливается на время - это нормально.
  //   Когда шарик отображается у левой стенки, это значит, что он находится на 0-7 X координате.
  //   Чтобы отбиться от стенки, он должен пройти от 7 до 0 и обратно от 0 до 7, 
  //   то есть отскок занимает в два раза больше времени, чем просто пролет через клетку.
  //   На высоких шарик телепортируется.
  //   Побитовое округление (или типо того). Округляет 7 до 8...
  //   Побитовое округление (или типо того). Округляет 7 до 8...
endmodule
